// Logisim project TTL-Computer.circ as structural Verilog: 9 circuits, main circuit main
module main (
  input  [7:0] DATA_BUS__IN,
  input  CLOCK_HALT,
  input  A_DATA_OUT,
  input  A_DATA_LOAD,
  input  B_DATA_OUT,
  input  B_DATA_LOAD,
  input  C_DATA_OUT,
  input  C_DATA_LOAD,
  input  [7:0] MANUAL_DATA,
  input  D_DATA_OUT,
  input  D_DATA_LOAD,
  input  FLAGS_LOAD,
  input  IR_LOAD,
  input  PC_INC,
  input  PC_DEC,
  input  PC_L_LOAD,
  input  PC_H_LOAD,
  input  PC_L_OUT,
  input  PC_H_OUT,
  input  STK_INC,
  input  STK_DEC,
  input  STK_RESET,
  input  ALU_A_IN,
  input  ALU_B_IN,
  input  ALU_S0,
  input  ALU_S1,
  input  ALU_S2,
  input  ALU_S3,
  input  ALU_M,
  input  ALU_Cn,
  input  ALU_OUT,
  input  MAR_LB_LOAD,
  input  MAR_HB_LOAD,
  input  MAR_PC_LOAD,
  input  MAR_STK_LOAD,
  input  MEM_BOOT_ROM,
  input  MEM_PROGRAM_ROM,
  input  MEM_RAM_LOAD,
  input  MEM_OUT,
  output [7:0] DATA_BUS__OUT,
  output Fgt,
  output Feq,
  output Flt,
  output Fz,
  output Fc
);

  wire and_1_out, CLOCK_64X, clock_divider_1_clock_div64, nA_DATA_LOAD, nA_DATA_OUT, nALU_A_IN, nALU_B_IN,
       nALU_OUT, nB_DATA_LOAD, nB_DATA_OUT, nC_DATA_LOAD, nC_DATA_OUT, nD_DATA_LOAD, nD_DATA_OUT,
       nFLAGS_LOAD, nIR_LOAD, nMAR_HB_LOAD, nMAR_LB_LOAD, nMAR_PC_LOAD, nMAR_STK_LOAD, nMEM_OUT,
       nMEM_RAM_LOAD, not_25_out, nPC_H_LOAD, nPC_H_OUT, nPC_L_LOAD, nPC_L_OUT, nSTK_RESET;
  wire [3:0] ALU_contents_bus_out, ALU_contents_bus_out_2, Memory_Access_Register_data_out,
       Memory_Access_Register_data_out_2, Memory_Access_Register_data_out_3,
       Memory_Access_Register_data_out_4, Memory_contents_out, Memory_contents_out_2,
       Program_Counter_mar_bus_out, Program_Counter_mar_bus_out_2, Program_Counter_mar_bus_out_3,
       Program_Counter_mar_bus_out_4, Register_A_contents_bus_out, Register_A_contents_bus_out_2,
       Register_B_contents_bus_out, Register_B_contents_bus_out_2, Register_C_contents_bus_out,
       Register_C_contents_bus_out_2, Register_D_contents_bus_out, Register_D_contents_bus_out_2;
  wire [4:0] ALU_fc;
  wire [7:0] Flags_Register_data_bus_out, Instruction_Register_contents_bus_out;
  wire [7:5] Flags_Register_contents_bus_out;
  wire [15:0] Stack_Pointer_mar_bus_out;

  Clock clock_1 (.out(CLOCK_64X));
  not not_1 (nA_DATA_OUT, A_DATA_OUT);
  not not_2 (nA_DATA_LOAD, A_DATA_LOAD);
  not not_3 (nB_DATA_OUT, B_DATA_OUT);
  not not_4 (nB_DATA_LOAD, B_DATA_LOAD);
  not not_5 (nC_DATA_OUT, C_DATA_OUT);
  not not_6 (nC_DATA_LOAD, C_DATA_LOAD);
  not not_7 (nD_DATA_OUT, D_DATA_OUT);
  not not_8 (nD_DATA_LOAD, D_DATA_LOAD);
  not not_9 (nFLAGS_LOAD, FLAGS_LOAD);
  not not_10 (nIR_LOAD, IR_LOAD);
  not not_11 (nPC_L_LOAD, PC_L_LOAD);
  not not_12 (nPC_H_LOAD, PC_H_LOAD);
  not not_13 (nPC_L_OUT, PC_L_OUT);
  not not_14 (nPC_H_OUT, PC_H_OUT);
  not not_15 (nSTK_RESET, STK_RESET);
  not not_16 (nALU_A_IN, ALU_A_IN);
  not not_17 (nALU_B_IN, ALU_B_IN);
  not not_18 (nALU_OUT, ALU_OUT);
  not not_19 (nMAR_LB_LOAD, MAR_LB_LOAD);
  not not_20 (nMAR_HB_LOAD, MAR_HB_LOAD);
  not not_21 (nMAR_PC_LOAD, MAR_PC_LOAD);
  not not_22 (nMAR_STK_LOAD, MAR_STK_LOAD);
  not not_23 (nMEM_RAM_LOAD, MEM_RAM_LOAD);
  not not_24 (nMEM_OUT, MEM_OUT);
  Hex_Digit_Display hex_digit_display_1 (.value(DATA_BUS__IN[7:4]));  // open: dp
  Hex_Digit_Display hex_digit_display_2 (.value(DATA_BUS__IN[3:0]));  // open: dp
  Hex_Digit_Display hex_digit_display_3 (.value(Program_Counter_mar_bus_out_4));  // open: dp
  Hex_Digit_Display hex_digit_display_4 (.value(Program_Counter_mar_bus_out_3));  // open: dp
  not not_25 (not_25_out, CLOCK_HALT);
  Clock_Divider clock_divider_1 (.CLOCK(CLOCK_64X), .CLOCK_DIV64(clock_divider_1_clock_div64));
  Hex_Digit_Display hex_digit_display_5 (.value(Register_C_contents_bus_out_2));  // open: dp
  Hex_Digit_Display hex_digit_display_6 (.value(Register_C_contents_bus_out));  // open: dp
  Register Register_C (
    .CLOCK(and_1_out), .nDATA_OUT(nC_DATA_OUT), .nDATA_LOAD(nC_DATA_LOAD),
    .CONTENTS_BUS_OUT({Register_C_contents_bus_out_2, Register_C_contents_bus_out}),
    .DATA_BUS_OUT(DATA_BUS__IN), .DATA_BUS_IN(DATA_BUS__IN));
  Hex_Digit_Display hex_digit_display_7 (.value(Program_Counter_mar_bus_out));  // open: dp
  Hex_Digit_Display hex_digit_display_8 (.value(Program_Counter_mar_bus_out_2));  // open: dp
  Hex_Digit_Display hex_digit_display_9 (.value(Register_D_contents_bus_out_2));  // open: dp
  Hex_Digit_Display hex_digit_display_10 (.value(Register_D_contents_bus_out));  // open: dp
  Register Register_D (
    .CLOCK(and_1_out), .nDATA_OUT(nD_DATA_OUT), .nDATA_LOAD(nD_DATA_LOAD),
    .CONTENTS_BUS_OUT({Register_D_contents_bus_out_2, Register_D_contents_bus_out}),
    .DATA_BUS_OUT(DATA_BUS__IN), .DATA_BUS_IN(DATA_BUS__IN));
  Hex_Digit_Display hex_digit_display_11 (.value(Register_A_contents_bus_out));  // open: dp
  Hex_Digit_Display hex_digit_display_12 (.value(Register_A_contents_bus_out_2));  // open: dp
  Register Register_A (
    .CLOCK(and_1_out), .nDATA_OUT(nA_DATA_OUT), .nDATA_LOAD(nA_DATA_LOAD),
    .CONTENTS_BUS_OUT({Register_A_contents_bus_out_2, Register_A_contents_bus_out}),
    .DATA_BUS_OUT(DATA_BUS__IN), .DATA_BUS_IN(DATA_BUS__IN));
  Hex_Digit_Display hex_digit_display_13 (.value(Register_B_contents_bus_out_2));  // open: dp
  Hex_Digit_Display hex_digit_display_14 (.value(Register_B_contents_bus_out));  // open: dp
  Register Register_B (
    .CLOCK(and_1_out), .nDATA_OUT(nB_DATA_OUT), .nDATA_LOAD(nB_DATA_LOAD),
    .CONTENTS_BUS_OUT({Register_B_contents_bus_out_2, Register_B_contents_bus_out}),
    .DATA_BUS_OUT(DATA_BUS__IN), .DATA_BUS_IN(DATA_BUS__IN));
  and and_1 (and_1_out, not_25_out, clock_divider_1_clock_div64);
  Program_Counter Program_Counter (
    .PC_INC(PC_INC), .PC_DEC(PC_DEC), .CLOCK(and_1_out), .PC_L_DATA_IN(DATA_BUS__IN),
    .nPC_L_LOAD(nPC_L_LOAD), .PC_H_DATA_IN(DATA_BUS__IN), .nPC_H_LOAD(nPC_H_LOAD),
    .MAR_BUS_OUT({Program_Counter_mar_bus_out_4, Program_Counter_mar_bus_out_3, Program_Counter_mar_bus_out_2, Program_Counter_mar_bus_out}),
    .nPC_L_OUT(nPC_L_OUT), .PC_L_DATA_OUT(DATA_BUS__IN), .PC_H_DATA_OUT(DATA_BUS__IN), .nPC_H_OUT(nPC_H_OUT));
  Register Flags_Register (
    .CLOCK(and_1_out), .nDATA_OUT(1'b0), .nDATA_LOAD(nFLAGS_LOAD),
    .CONTENTS_BUS_OUT({Flags_Register_contents_bus_out, Fgt, Feq, Flt, Fz, Fc}),
    .DATA_BUS_OUT(Flags_Register_data_bus_out), .DATA_BUS_IN({3'b000, ALU_fc}));
  Hex_Digit_Display hex_digit_display_15 (.value(Stack_Pointer_mar_bus_out[15:12]));  // open: dp
  Stack_Pointer Stack_Pointer (
    .STK_DEC(STK_DEC), .CLOCK(and_1_out), .nSTK_RESET(nSTK_RESET), .MAR_BUS_OUT(Stack_Pointer_mar_bus_out),
    .STK_INC(STK_INC));
  Hex_Digit_Display hex_digit_display_16 (.value(Memory_Access_Register_data_out_4));  // open: dp
  Memory_Access_Register Memory_Access_Register (
    .LB_DATA_IN(DATA_BUS__IN), .CLOCK(and_1_out), .nLB_LOAD(nMAR_LB_LOAD), .HB_DATA_IN(DATA_BUS__IN),
    .nHB_LOAD(nMAR_HB_LOAD),
    .PC_DATA_IN({Program_Counter_mar_bus_out_4, Program_Counter_mar_bus_out_3, Program_Counter_mar_bus_out_2, Program_Counter_mar_bus_out}),
    .STK_DATA_IN(Stack_Pointer_mar_bus_out), .nPC_LOAD(nMAR_PC_LOAD), .nSTK_LOAD(nMAR_STK_LOAD),
    .DATA_OUT({Memory_Access_Register_data_out_4, Memory_Access_Register_data_out_3, Memory_Access_Register_data_out_2, Memory_Access_Register_data_out}));
  ALU ALU (
    .DATA_BUS_IN(DATA_BUS__IN), .CLOCK(and_1_out), .nA_IN(nALU_A_IN), .nB_IN(nALU_B_IN), .S3(ALU_S3),
    .S2(ALU_S2), .S1(ALU_S1), .S0(ALU_S0), .M(ALU_M), .Cn(ALU_Cn), .nALU_OUT(nALU_OUT), .Flt(ALU_fc[2]),
    .Feq(ALU_fc[3]), .Fgt(ALU_fc[4]), .DATA_BUS_OUT(DATA_BUS__IN), .Fc(ALU_fc[0]),
    .CONTENTS_BUS_OUT({ALU_contents_bus_out_2, ALU_contents_bus_out}), .Fz(ALU_fc[1]));
  Hex_Digit_Display hex_digit_display_17 (.value(Stack_Pointer_mar_bus_out[7:4]));  // open: dp
  Hex_Digit_Display hex_digit_display_18 (.value(Stack_Pointer_mar_bus_out[11:8]));  // open: dp
  Hex_Digit_Display hex_digit_display_19 (.value(Memory_Access_Register_data_out_2));  // open: dp
  Hex_Digit_Display hex_digit_display_20 (.value(Memory_Access_Register_data_out_3));  // open: dp
  Hex_Digit_Display hex_digit_display_21 (.value(ALU_contents_bus_out_2));  // open: dp
  Hex_Digit_Display hex_digit_display_22 (.value(ALU_contents_bus_out));  // open: dp
  Hex_Digit_Display hex_digit_display_23 (.value(Stack_Pointer_mar_bus_out[3:0]));  // open: dp
  Hex_Digit_Display hex_digit_display_24 (.value(Memory_Access_Register_data_out));  // open: dp
  DotMatrix #(.matrixcols(6), .matrixrows(1), .dotshape("circle")) dotmatrix_1 (
    .col0(Instruction_Register_contents_bus_out[5]), .col1(Instruction_Register_contents_bus_out[4]),
    .col2(Instruction_Register_contents_bus_out[3]), .col3(Instruction_Register_contents_bus_out[2]),
    .col4(Instruction_Register_contents_bus_out[1]), .col5(Instruction_Register_contents_bus_out[0]));
  Hex_Digit_Display hex_digit_display_25 (.value(Instruction_Register_contents_bus_out[7:4]));  // open: dp
  Hex_Digit_Display hex_digit_display_26 (.value(Instruction_Register_contents_bus_out[3:0]));  // open: dp
  Register Instruction_Register (
    .CLOCK(and_1_out), .nDATA_OUT(1'b0), .nDATA_LOAD(nIR_LOAD),
    .CONTENTS_BUS_OUT(Instruction_Register_contents_bus_out), .DATA_BUS_IN(DATA_BUS__IN));  // open: DATA_BUS_OUT
  Hex_Digit_Display hex_digit_display_27 (.value(Memory_contents_out_2));  // open: dp
  Memory Memory (
    .BOOT_ROM(MEM_BOOT_ROM), .PROGRAM_RAM(MEM_PROGRAM_ROM), .nRAM_LOAD(nMEM_RAM_LOAD), .nMEM_OUT(nMEM_OUT),
    .CLOCK(and_1_out), .DATA_IN(DATA_BUS__IN), .MANUAL_DATA_IN(MANUAL_DATA), .DATA_OUT(DATA_BUS__IN),
    .ADDRESS_IN({Memory_Access_Register_data_out_4, Memory_Access_Register_data_out_3, Memory_Access_Register_data_out_2, Memory_Access_Register_data_out}),
    .CONTENTS_OUT({Memory_contents_out_2, Memory_contents_out}));
  Hex_Digit_Display hex_digit_display_28 (.value(Memory_contents_out));  // open: dp

  assign DATA_BUS__OUT = DATA_BUS__IN;

  // Other names for the same wires on the sheet: MEM_PROGRAM_RAM = MEM_PROGRAM_ROM

  // Notes on the sheet:
  //   ~FLAGS_OUT
  //   Create separate input selector per flag?
  //   Flags output
endmodule

module Register (
  input  [7:0] DATA_BUS_IN,
  input  CLOCK,
  input  nDATA_LOAD,
  input  nDATA_OUT,
  output [7:0] CONTENTS_BUS_OUT,
  output [7:0] DATA_BUS_OUT
);

  // IC_74377 ic_74377_1: pin names not known; wires that end beside it: CLOCK, nDATA_LOAD, CONTENTS_BUS_OUT[0], CONTENTS_BUS_OUT[1], CONTENTS_BUS_OUT[2], CONTENTS_BUS_OUT[3], CONTENTS_BUS_OUT[4], CONTENTS_BUS_OUT[5], CONTENTS_BUS_OUT[6], CONTENTS_BUS_OUT[7]
  // IC_74244 ic_74244_1: pin names not known; wires that end beside it: CONTENTS_BUS_OUT[0], CONTENTS_BUS_OUT[1], CONTENTS_BUS_OUT[2], CONTENTS_BUS_OUT[3], CONTENTS_BUS_OUT[4], CONTENTS_BUS_OUT[5], CONTENTS_BUS_OUT[6], CONTENTS_BUS_OUT[7], nDATA_OUT, nDATA_OUT, DATA_BUS_OUT[0], DATA_BUS_OUT[1], DATA_BUS_OUT[2], DATA_BUS_OUT[3], DATA_BUS_OUT[4], DATA_BUS_OUT[5], DATA_BUS_OUT[6], DATA_BUS_OUT[7]
endmodule

module Program_Counter (
  input  PC_INC,
  input  PC_DEC,
  input  CLOCK,
  input  [7:0] PC_L_DATA_IN,
  input  nPC_L_OUT,
  input  nPC_L_LOAD,
  input  [7:0] PC_H_DATA_IN,
  input  nPC_H_OUT,
  input  nPC_H_LOAD,
  output [7:0] PC_L_DATA_OUT,
  output [15:0] MAR_BUS_OUT,
  output [7:0] PC_H_DATA_OUT
);

  wire DOWN_nUP, n74191_1_nrco, n74191_2_nrco, n74191_3_nrco, nCLK_EN, nor_2_out;

  nor nor_1 (DOWN_nUP, PC_INC, nor_2_out);
  nor nor_2 (nor_2_out, DOWN_nUP, PC_DEC);
  nor nor_3 (nCLK_EN, PC_INC, PC_DEC);
  _74191 u_74191_1 (
    .nU_D(DOWN_nUP), .CK(CLOCK), .nCTEN(nCLK_EN), .nPL(nPC_L_LOAD), .Q0(MAR_BUS_OUT[0]), .Q1(MAR_BUS_OUT[1]),
    .Q2(MAR_BUS_OUT[2]), .Q3(MAR_BUS_OUT[3]), .D0(PC_L_DATA_IN[0]), .D1(PC_L_DATA_IN[1]),
    .D2(PC_L_DATA_IN[2]), .D3(PC_L_DATA_IN[3]), .nRCO(n74191_1_nrco));  // open: TC
  _74191 u_74191_2 (
    .nU_D(DOWN_nUP), .CK(n74191_1_nrco), .nCTEN(nCLK_EN), .nPL(nPC_L_LOAD), .Q0(MAR_BUS_OUT[4]),
    .Q1(MAR_BUS_OUT[5]), .Q2(MAR_BUS_OUT[6]), .Q3(MAR_BUS_OUT[7]), .D0(PC_L_DATA_IN[4]),
    .D1(PC_L_DATA_IN[5]), .D2(PC_L_DATA_IN[6]), .D3(PC_L_DATA_IN[7]), .nRCO(n74191_2_nrco));  // open: TC
  _74191 u_74191_3 (
    .nU_D(DOWN_nUP), .CK(n74191_2_nrco), .nCTEN(nCLK_EN), .nPL(nPC_H_LOAD), .Q0(MAR_BUS_OUT[8]),
    .Q1(MAR_BUS_OUT[9]), .Q2(MAR_BUS_OUT[10]), .Q3(MAR_BUS_OUT[11]), .D0(PC_H_DATA_IN[0]),
    .D1(PC_H_DATA_IN[1]), .D2(PC_H_DATA_IN[2]), .D3(PC_H_DATA_IN[3]), .nRCO(n74191_3_nrco));  // open: TC
  _74191 u_74191_4 (
    .nU_D(DOWN_nUP), .CK(n74191_3_nrco), .nCTEN(nCLK_EN), .nPL(nPC_H_LOAD), .Q0(MAR_BUS_OUT[12]),
    .Q1(MAR_BUS_OUT[13]), .Q2(MAR_BUS_OUT[14]), .Q3(MAR_BUS_OUT[15]), .D0(PC_H_DATA_IN[4]),
    .D1(PC_H_DATA_IN[5]), .D2(PC_H_DATA_IN[6]), .D3(PC_H_DATA_IN[7]));  // open: TC, nRCO
  // IC_74244 ic_74244_1: pin names not known; wires that end beside it: MAR_BUS_OUT[0], MAR_BUS_OUT[1], MAR_BUS_OUT[2], MAR_BUS_OUT[3], MAR_BUS_OUT[4], MAR_BUS_OUT[5], MAR_BUS_OUT[6], MAR_BUS_OUT[7], nPC_L_OUT, nPC_L_OUT, PC_L_DATA_OUT[0], PC_L_DATA_OUT[1], PC_L_DATA_OUT[2], PC_L_DATA_OUT[3], PC_L_DATA_OUT[4], PC_L_DATA_OUT[5], PC_L_DATA_OUT[6], PC_L_DATA_OUT[7]
  // IC_74244 ic_74244_2: pin names not known; wires that end beside it: MAR_BUS_OUT[8], MAR_BUS_OUT[9], MAR_BUS_OUT[10], MAR_BUS_OUT[11], MAR_BUS_OUT[12], MAR_BUS_OUT[13], MAR_BUS_OUT[14], MAR_BUS_OUT[15], nPC_H_OUT, nPC_H_OUT, PC_H_DATA_OUT[0], PC_H_DATA_OUT[1], PC_H_DATA_OUT[2], PC_H_DATA_OUT[3], PC_H_DATA_OUT[4], PC_H_DATA_OUT[5], PC_H_DATA_OUT[6], PC_H_DATA_OUT[7]
endmodule

module Sequencer_Instruction_Decoder (
  input  nOE,
  input  RESTART,
  input  LOAD,
  output nA_DATA_OUT,
  output nA_DATA_LOAD,
  output nB_DATA_OUT,
  output nB_DATA_LOAD,
  output nC_DATA_OUT,
  output nC_DATA_LOAD,
  output nD_DATA_OUT,
  output nD_DATA_LOAD,
  output nFLAGS_LOAD,
  output nIR_LOAD,
  output PC_INC,
  output PC_DEC,
  output nPC_L_LOAD,
  output nPC_H_LOAD,
  output nPC_L_OUT,
  output nPC_H_OUT,
  output STK_INC,
  output STK_DEC,
  output nSTK_RESET,
  output nALU_A_IN,
  output nALU_B_IN,
  output ALU_S0,
  output ALU_S1,
  output ALU_S2,
  output ALU_S3,
  output ALU_M,
  output ALU_Cn,
  output nALU_OUT
);

  wire A_DATA_LOAD, A_DATA_OUT, ALU_A_IN, ALU_B_IN, ALU_OUT, and_1_out, and_3_out, and_4_out, and_5_out,
       B_DATA_LOAD, B_DATA_OUT, C_DATA_LOAD, C_DATA_OUT, CLOCK_out, D_DATA_LOAD, D_DATA_OUT, dip_7474_1_p1,
       dip_7474_1_p2, dip_7474_1_p4, dip_74161_1_p3, dip_74161_1_p5, dip_74161_1_p7, dip_74161_1_p9,
       dip_74161_1_p13, dip_74161_2_p1, dip_74161_2_p2, dip_74161_2_p9, dip_74161_2_p13, dip_74595_1_p2,
       dip_74595_1_p6, dip_74595_1_p10, dip_74595_2_p6, dip_74595_3_p6, dip_74595_4_p6, dip_74595_5_p6,
       FLAGS_LOAD, IR_LOAD, n74165_1_p1, n74165_1_p2, n74165_1_p13, not_19_out, not_20_out, not_22_out,
       not_25_out, not_26_out, or_1_out, or_2_out, or_3_out, PC_H_LOAD, PC_H_OUT, PC_L_LOAD, PC_L_OUT,
       STK_RESET;
  wire [2:0] dip_74161_2_p3;
  wire [3:0] dip_74595_1_p7, dip_74595_1_p12, dip_74595_2_p3, dip_74595_2_p8, dip_74595_3_p3, dip_74595_3_p8,
       dip_74595_4_p3, dip_74595_4_p8, dip_74595_5_p3, dip_74595_5_p8, dip_74595_6_p3, dip_74595_6_p8;
  wire [7:0] rom_1_data;

  not not_1 (nA_DATA_OUT, A_DATA_OUT);
  not not_2 (nA_DATA_LOAD, A_DATA_LOAD);
  not not_3 (nB_DATA_OUT, B_DATA_OUT);
  not not_4 (nB_DATA_LOAD, B_DATA_LOAD);
  not not_5 (nC_DATA_OUT, C_DATA_OUT);
  not not_6 (nC_DATA_LOAD, C_DATA_LOAD);
  not not_7 (nD_DATA_OUT, D_DATA_OUT);
  not not_8 (nD_DATA_LOAD, D_DATA_LOAD);
  not not_9 (nFLAGS_LOAD, FLAGS_LOAD);
  not not_10 (nIR_LOAD, IR_LOAD);
  not not_11 (nPC_L_LOAD, PC_L_LOAD);
  not not_12 (nPC_H_LOAD, PC_H_LOAD);
  not not_13 (nPC_L_OUT, PC_L_OUT);
  not not_14 (nPC_H_OUT, PC_H_OUT);
  not not_15 (nSTK_RESET, STK_RESET);
  not not_16 (nALU_A_IN, ALU_A_IN);
  not not_17 (nALU_B_IN, ALU_B_IN);
  not not_18 (nALU_OUT, ALU_OUT);
  ROM #(.addrWidth(19)) rom_1 (.addr({{16{1'b0}}, dip_74161_2_p3}), .data(rom_1_data), .sel(1'b1));
  // _74165 74165_1: pin names not known; wires that end beside it: n74165_1_p1, n74165_1_p2, rom_1_data[4], rom_1_data[5], rom_1_data[6], rom_1_data[7], 1'b0, rom_1_data[3], rom_1_data[2], rom_1_data[1], rom_1_data[0], 1'b0, n74165_1_p13
  nor nor_1 (n74165_1_p1, LOAD, and_1_out);
  Hex_Digit_Display hex_digit_display_1 (.value(dip_74595_1_p7));  // open: dp
  DotMatrix #(.matrixcols(24), .matrixrows(1), .dotshape("circle")) dotmatrix_1 (
    .col0(dip_74595_1_p7[3]), .col1(dip_74595_1_p7[2]), .col2(dip_74595_1_p7[1]), .col3(dip_74595_1_p7[0]),
    .col4(dip_74595_1_p12[3]), .col5(dip_74595_1_p12[2]), .col6(dip_74595_1_p12[1]),
    .col7(dip_74595_1_p12[0]), .col8(dip_74595_2_p3[3]), .col9(dip_74595_2_p3[2]), .col10(dip_74595_2_p3[1]),
    .col11(dip_74595_2_p3[0]), .col12(dip_74595_2_p8[3]), .col13(dip_74595_2_p8[2]),
    .col14(dip_74595_2_p8[1]), .col15(dip_74595_2_p8[0]), .col16(dip_74595_3_p3[3]),
    .col17(dip_74595_3_p3[2]), .col18(dip_74595_3_p3[1]), .col19(dip_74595_3_p3[0]),
    .col20(dip_74595_3_p8[3]), .col21(dip_74595_3_p8[2]), .col22(dip_74595_3_p8[1]), .col23(dip_74595_3_p8[0]));
  Hex_Digit_Display hex_digit_display_2 (.value(dip_74595_2_p3));  // open: dp
  Hex_Digit_Display hex_digit_display_3 (.value(dip_74595_1_p12));  // open: dp
  // DIP_74595 dip_74595_1: pin names not known; wires that end beside it: dip_74595_1_p7[3], dip_74595_1_p2, dip_74595_1_p7[2], n74165_1_p2, dip_74595_1_p7[1], dip_74595_1_p6, dip_74595_1_p7[0], nOE, dip_74595_1_p12[3], dip_74595_1_p10, dip_74595_1_p12[2], dip_74595_1_p12[0], dip_74595_1_p12[1], dip_74595_1_p10, dip_74595_2_p3[3], dip_74595_1_p2, dip_74595_2_p3[2], n74165_1_p2
  Hex_Digit_Display hex_digit_display_4 (.value(dip_74595_2_p8));  // open: dp
  Hex_Digit_Display hex_digit_display_5 (.value(dip_74595_3_p3));  // open: dp
  // DIP_74595 dip_74595_2: pin names not known; wires that end beside it: dip_74595_2_p3[1], dip_74595_1_p6, dip_74595_2_p3[0], nOE, dip_74595_2_p8[3], dip_74595_2_p6, dip_74595_2_p8[2], dip_74595_2_p8[0], dip_74595_2_p8[1], dip_74595_2_p6, dip_74595_3_p3[3], dip_74595_1_p2, dip_74595_3_p3[2], n74165_1_p2
  Hex_Digit_Display hex_digit_display_6 (.value(dip_74595_3_p8));  // open: dp
  DotMatrix #(.matrixcols(24), .matrixrows(1), .dotshape("circle")) dotmatrix_2 (
    .col0(dip_74595_4_p3[3]), .col1(dip_74595_4_p3[2]), .col2(dip_74595_4_p3[1]), .col3(dip_74595_4_p3[0]),
    .col4(dip_74595_4_p8[3]), .col5(dip_74595_4_p8[2]), .col6(dip_74595_4_p8[1]), .col7(dip_74595_4_p8[0]),
    .col8(dip_74595_5_p3[3]), .col9(dip_74595_5_p3[2]), .col10(dip_74595_5_p3[1]), .col11(dip_74595_5_p3[0]),
    .col12(dip_74595_5_p8[3]), .col13(dip_74595_5_p8[2]), .col14(dip_74595_5_p8[1]),
    .col15(dip_74595_5_p8[0]), .col16(dip_74595_6_p3[3]), .col17(dip_74595_6_p3[2]),
    .col18(dip_74595_6_p3[1]), .col19(dip_74595_6_p3[0]), .col20(dip_74595_6_p8[3]),
    .col21(dip_74595_6_p8[2]), .col22(dip_74595_6_p8[1]), .col23(dip_74595_6_p8[0]));
  // DIP_74595 dip_74595_3: pin names not known; wires that end beside it: dip_74595_3_p3[1], dip_74595_1_p6, dip_74595_3_p3[0], nOE, dip_74595_3_p8[3], dip_74595_3_p6, dip_74595_3_p8[2], dip_74595_3_p8[0], dip_74595_3_p8[1], dip_74595_3_p6, dip_74595_4_p3[3], dip_74595_1_p2, dip_74595_4_p3[2], n74165_1_p2
  and and_1 (and_1_out, and_4_out, CLOCK_out);
  Hex_Digit_Display hex_digit_display_7 (.value(dip_74595_4_p8));  // open: dp
  Hex_Digit_Display hex_digit_display_8 (.value(dip_74595_4_p3));  // open: dp
  // DIP_74595 dip_74595_4: pin names not known; wires that end beside it: dip_74595_4_p3[1], dip_74595_1_p6, dip_74595_4_p3[0], nOE, dip_74595_4_p8[3], dip_74595_4_p6, dip_74595_4_p8[2], dip_74595_4_p8[0], dip_74595_4_p8[1], dip_74595_4_p6, dip_74595_5_p3[3], dip_74595_1_p2, dip_74595_5_p3[2], n74165_1_p2
  nor nor_2 (dip_74595_1_p2, n74165_1_p1, or_1_out);
  or or_1 (or_1_out, and_4_out, not_19_out);
  not not_19 (not_19_out, CLOCK_out);
  Hex_Digit_Display hex_digit_display_9 (.value(dip_74595_5_p8));  // open: dp
  Hex_Digit_Display hex_digit_display_10 (.value(dip_74595_5_p3));  // open: dp
  // DIP_74595 dip_74595_5: pin names not known; wires that end beside it: dip_74595_5_p3[1], dip_74595_1_p6, dip_74595_5_p3[0], nOE, dip_74595_5_p8[3], dip_74595_5_p6, dip_74595_5_p8[2], dip_74595_5_p8[0], dip_74595_5_p8[1], dip_74595_5_p6, dip_74595_6_p3[3], dip_74595_1_p2, dip_74595_6_p3[2], n74165_1_p2
  and and_2 (n74165_1_p2, and_3_out, not_20_out);
  not not_20 (not_20_out, and_5_out);
  and and_3 (and_3_out, or_2_out, CLOCK_out);
  or or_2 (or_2_out, n74165_1_p1, and_4_out);
  Clock CLOCK (.out(CLOCK_out));
  Hex_Digit_Display hex_digit_display_11 (.value(dip_74595_6_p8));  // open: dp
  Hex_Digit_Display hex_digit_display_12 (.value(dip_74595_6_p3));  // open: dp
  // DIP_74595 dip_74595_6: pin names not known; wires that end beside it: dip_74595_6_p3[1], dip_74595_1_p6, dip_74595_6_p3[0], nOE, dip_74595_6_p8[3], n74165_1_p13, dip_74595_6_p8[2], dip_74595_6_p8[0], dip_74595_6_p8[1]
  not not_21 (dip_74595_1_p6, n74165_1_p2);
  and and_4 (and_4_out, dip_74161_1_p3, dip_74161_1_p5, dip_74161_1_p7);
  or or_3 (or_3_out, and_4_out, n74165_1_p1);
  and and_5 (and_5_out, dip_7474_1_p4, not_22_out);
  DotMatrix #(.matrixcols(4), .matrixrows(1), .dotshape("circle")) dotmatrix_3 (
    .col0(dip_74161_1_p9), .col1(dip_74161_1_p7), .col2(dip_74161_1_p5), .col3(dip_74161_1_p3));
  // DIP_74161 dip_74161_1: pin names not known; wires that end beside it: or_3_out, n74165_1_p2, dip_74161_1_p3, 1'b0, dip_74161_1_p5, 1'b0, dip_74161_1_p7, 1'b0, dip_74161_1_p9, 1'b0, 1'b1, 1'b1, dip_74161_1_p13
  not not_22 (not_22_out, LOAD);
  not not_23 (dip_74161_1_p13, and_4_out);
  DotMatrix #(.matrixcols(4), .matrixrows(1), .dotshape("circle")) dotmatrix_4 (
    .col0(dip_74161_2_p9), .col1(dip_74161_2_p3[2]), .col2(dip_74161_2_p3[1]), .col3(dip_74161_2_p3[0]));
  // DIP_74161 dip_74161_2: pin names not known; wires that end beside it: dip_74161_2_p1, dip_74161_2_p2, dip_74161_2_p3[0], 1'b0, dip_74161_2_p3[1], 1'b0, dip_74161_2_p3[2], 1'b0, dip_74161_2_p9, 1'b0, 1'b1, 1'b1, dip_74161_2_p13
  not not_24 (dip_74161_2_p1, dip_74595_1_p2);
  // Probe on dip_74161_2_p2
  // AND_Gate and_6 has open pins: in1=n74165_1_p2, out=open
  not not_25 (not_25_out, and_4_out);
  nor nor_3 (dip_74161_2_p2, not_25_out, n74165_1_p2, not_26_out);
  not not_26 (not_26_out, CLOCK_out);
  // DIP_7474 dip_7474_1: pin names not known; wires that end beside it: dip_7474_1_p1, dip_7474_1_p2, dip_7474_1_p2, dip_7474_1_p4
  not not_27 (dip_7474_1_p1, LOAD);
  and and_7 (dip_7474_1_p2, dip_74161_2_p3[1], dip_74161_2_p3[2]);
  not not_28 (dip_74161_2_p13, RESTART);

  // Notes on the sheet:
  //   LOAD: pull=down
  //   RESTART: pull=down
  //   nOE: pull=down
  //   CONTROL ROM
  //   ROM DATA
  //   contents of rom_1 (hex, n*v repeats v):
  //   a3 b6 3c 1d e9 8f
  //   SH/~LR
  //   DATA
  //   NEXT_BIT
  //   ~CLR
  //   ~CLR
  //   SRCLK
  //   DATA
  //   RCLK
  //   CLR
  //   NEXT_BIT
  //   DONE
  //   DATA BIT COUNTER
  //   CE
  //   RESTART
  //   CLR
  //   DATA BYTE COUNTER
  //   CE
endmodule

module Stack_Pointer (
  input  STK_INC,
  input  STK_DEC,
  input  CLOCK,
  input  nSTK_RESET,
  output [15:0] MAR_BUS_OUT
);

  wire DOWN_nUP, n74191_1_nrco, nCLK_EN, nor_2_out;

  nor nor_1 (DOWN_nUP, STK_INC, nor_2_out);
  nor nor_2 (nor_2_out, DOWN_nUP, STK_DEC);
  nor nor_3 (nCLK_EN, STK_INC, STK_DEC);
  _74191 u_74191_1 (
    .nU_D(DOWN_nUP), .CK(CLOCK), .nCTEN(nCLK_EN), .nPL(nSTK_RESET), .Q0(MAR_BUS_OUT[0]), .Q1(MAR_BUS_OUT[1]),
    .Q2(MAR_BUS_OUT[2]), .Q3(MAR_BUS_OUT[3]), .D0(1'b0), .D1(1'b0), .D2(1'b0), .D3(1'b0), .nRCO(n74191_1_nrco));  // open: TC
  _74191 u_74191_2 (
    .nU_D(DOWN_nUP), .CK(n74191_1_nrco), .nCTEN(nCLK_EN), .nPL(nSTK_RESET), .Q0(MAR_BUS_OUT[4]),
    .Q1(MAR_BUS_OUT[5]), .Q2(MAR_BUS_OUT[6]), .Q3(MAR_BUS_OUT[7]), .D0(1'b0), .D1(1'b0), .D2(1'b0), .D3(1'b0));  // open: TC, nRCO

  assign MAR_BUS_OUT[15:8] = {8{1'b1}};
endmodule

module ALU (
  input  [7:0] DATA_BUS_IN,
  input  CLOCK,
  input  nA_IN,
  input  nB_IN,
  input  S3,
  input  S2,
  input  S1,
  input  S0,
  input  M,
  input  Cn,
  input  nALU_OUT,
  output Flt,
  output Feq,
  output Fgt,
  output [7:0] DATA_BUS_OUT,
  output Fc,
  output [7:0] CONTENTS_BUS_OUT,
  output Fz
);

  wire and_1_out, and_3_out, ic_74377_1_p1, ic_74377_1_p2, ic_74377_1_p3, ic_74377_1_p4, ic_74377_1_p5,
       ic_74377_1_p6, ic_74377_1_p7, ic_74377_1_p8, ic_74377_2_p5, ic_74377_2_p6, ic_74377_2_p7,
       ic_74377_2_p8, ic_74377_2_p9, ic_74377_2_p10, ic_74377_2_p11, ic_74377_2_p12, n74181_1_p18,
       n74181_1_p19, n74181_2_p18, n74181_2_p19, not_2_out, not_3_out;

  // IC_74377 ic_74377_1: pin names not known; wires that end beside it: ic_74377_1_p1, ic_74377_1_p2, ic_74377_1_p3, ic_74377_1_p4, ic_74377_1_p5, ic_74377_1_p6, ic_74377_1_p7, ic_74377_1_p8
  // IC_74377 ic_74377_2: pin names not known; wires that end beside it: CLOCK, nA_IN, CLOCK, nB_IN, ic_74377_2_p5, ic_74377_2_p6, ic_74377_2_p7, ic_74377_2_p8, ic_74377_2_p9, ic_74377_2_p10, ic_74377_2_p11, ic_74377_2_p12
  // _74181 74181_1: pin names not known; wires that end beside it: ic_74377_2_p5, ic_74377_1_p1, S3, S2, S1, S0, Cn, M, CONTENTS_BUS_OUT[0], CONTENTS_BUS_OUT[1], CONTENTS_BUS_OUT[2], ic_74377_1_p2, ic_74377_2_p6, ic_74377_1_p3, ic_74377_2_p7, ic_74377_1_p4, ic_74377_2_p8, n74181_1_p18, n74181_1_p19, CONTENTS_BUS_OUT[3]
  // _74181 74181_2: pin names not known; wires that end beside it: ic_74377_2_p9, ic_74377_1_p5, S3, S2, S1, S0, n74181_1_p18, M, CONTENTS_BUS_OUT[4], CONTENTS_BUS_OUT[5], CONTENTS_BUS_OUT[6], ic_74377_1_p6, ic_74377_2_p10, ic_74377_1_p7, ic_74377_2_p11, ic_74377_1_p8, ic_74377_2_p12, n74181_2_p18, n74181_2_p19, CONTENTS_BUS_OUT[7]
  not not_1 (Fc, n74181_2_p18);
  and and_1 (and_1_out, n74181_1_p18, n74181_2_p18);
  or or_1 (Flt, and_1_out, n74181_2_p18);
  and and_2 (Feq, n74181_1_p19, n74181_2_p19);
  not not_2 (not_2_out, n74181_1_p18);
  not not_3 (not_3_out, n74181_2_p18);
  and and_3 (and_3_out, not_2_out, not_3_out);
  or or_2 (Fgt, and_3_out, not_3_out);
  nor nor_1 (Fz, CONTENTS_BUS_OUT[0], CONTENTS_BUS_OUT[1], CONTENTS_BUS_OUT[2], CONTENTS_BUS_OUT[3], CONTENTS_BUS_OUT[4], CONTENTS_BUS_OUT[5], CONTENTS_BUS_OUT[6], CONTENTS_BUS_OUT[7]);
  // IC_74244 ic_74244_1: pin names not known; wires that end beside it: CONTENTS_BUS_OUT[0], CONTENTS_BUS_OUT[1], CONTENTS_BUS_OUT[2], CONTENTS_BUS_OUT[3], CONTENTS_BUS_OUT[4], CONTENTS_BUS_OUT[5], CONTENTS_BUS_OUT[6], CONTENTS_BUS_OUT[7], nALU_OUT, nALU_OUT, DATA_BUS_OUT[0], DATA_BUS_OUT[1], DATA_BUS_OUT[2], DATA_BUS_OUT[3], DATA_BUS_OUT[4], DATA_BUS_OUT[5], DATA_BUS_OUT[6], DATA_BUS_OUT[7]

  // Notes on the sheet:
  //   M=0   Cn=0   S=0110  (A < B)
  //   M=0   Cn=1   S=0110  (A=B)
  //   M=0   Cn=1   S=0110  (A>B)
endmodule

module Memory_Access_Register (
  input  [7:0] LB_DATA_IN,
  input  CLOCK,
  input  nLB_LOAD,
  input  [7:0] HB_DATA_IN,
  input  nHB_LOAD,
  input  [15:0] PC_DATA_IN,
  input  [15:0] STK_DATA_IN,
  input  nPC_LOAD,
  input  nSTK_LOAD,
  output [15:0] DATA_OUT
);

  wire and_1_out, and_3_out, High_byte_p13, High_byte_p14, High_byte_p15, High_byte_p16, High_byte_p17,
       High_byte_p18, High_byte_p19, High_byte_p20, Low_byte_p9, Low_byte_p10, Low_byte_p11, Low_byte_p12,
       Low_byte_p13, Low_byte_p14, Low_byte_p15, Low_byte_p16, nHIGH_LOAD, nLOW_LOAD;

  // IC_74244 Low_byte: pin names not known; wires that end beside it: LB_DATA_IN[0], LB_DATA_IN[1], LB_DATA_IN[2], LB_DATA_IN[3], LB_DATA_IN[4], LB_DATA_IN[5], LB_DATA_IN[6], LB_DATA_IN[7], Low_byte_p9, Low_byte_p10, Low_byte_p11, Low_byte_p12, Low_byte_p13, Low_byte_p14, Low_byte_p15, Low_byte_p16
  // IC_74244 High_byte: pin names not known; wires that end beside it: nLB_LOAD, nLB_LOAD, HB_DATA_IN[0], HB_DATA_IN[1], HB_DATA_IN[2], HB_DATA_IN[3], HB_DATA_IN[4], HB_DATA_IN[5], HB_DATA_IN[6], HB_DATA_IN[7], nHB_LOAD, nHB_LOAD, High_byte_p13, High_byte_p14, High_byte_p15, High_byte_p16, High_byte_p17, High_byte_p18, High_byte_p19, High_byte_p20
  // IC_74244 Low_byte_2: pin names not known; wires that end beside it: PC_DATA_IN[0], PC_DATA_IN[1], PC_DATA_IN[2], PC_DATA_IN[3], PC_DATA_IN[4], PC_DATA_IN[5], PC_DATA_IN[6], PC_DATA_IN[7], Low_byte_p9, Low_byte_p10, Low_byte_p11, Low_byte_p12, Low_byte_p13, Low_byte_p14, Low_byte_p15, Low_byte_p16
  // IC_74244 High_byte_2: pin names not known; wires that end beside it: nPC_LOAD, nPC_LOAD, PC_DATA_IN[8], PC_DATA_IN[9], PC_DATA_IN[10], PC_DATA_IN[11], PC_DATA_IN[12], PC_DATA_IN[13], PC_DATA_IN[14], PC_DATA_IN[15], nPC_LOAD, nPC_LOAD, High_byte_p13, High_byte_p14, High_byte_p15, High_byte_p16, High_byte_p17, High_byte_p18, High_byte_p19, High_byte_p20
  // IC_74244 Low_byte_3: pin names not known; wires that end beside it: STK_DATA_IN[0], STK_DATA_IN[1], STK_DATA_IN[2], STK_DATA_IN[3], STK_DATA_IN[4], STK_DATA_IN[5], STK_DATA_IN[6], STK_DATA_IN[7], Low_byte_p9, Low_byte_p10, Low_byte_p11, Low_byte_p12, Low_byte_p13, Low_byte_p14, Low_byte_p15, Low_byte_p16
  // IC_74244 High_byte_3: pin names not known; wires that end beside it: nSTK_LOAD, nSTK_LOAD, STK_DATA_IN[8], STK_DATA_IN[9], STK_DATA_IN[10], STK_DATA_IN[11], STK_DATA_IN[12], STK_DATA_IN[13], STK_DATA_IN[14], STK_DATA_IN[15], nSTK_LOAD, nSTK_LOAD, High_byte_p13, High_byte_p14, High_byte_p15, High_byte_p16, High_byte_p17, High_byte_p18, High_byte_p19, High_byte_p20
  // IC_74377 Low_byte_4: pin names not known; wires that end beside it: Low_byte_p9, Low_byte_p10, Low_byte_p11, Low_byte_p12, Low_byte_p13, Low_byte_p14, Low_byte_p15, Low_byte_p16, DATA_OUT[0], DATA_OUT[1], DATA_OUT[2], DATA_OUT[3], DATA_OUT[4], DATA_OUT[5], DATA_OUT[6], DATA_OUT[7]
  // IC_74377 High_byte_4: pin names not known; wires that end beside it: CLOCK, nLOW_LOAD, High_byte_p13, High_byte_p14, High_byte_p15, High_byte_p16, High_byte_p17, High_byte_p18, High_byte_p19, High_byte_p20, CLOCK, nHIGH_LOAD, DATA_OUT[8], DATA_OUT[9], DATA_OUT[10], DATA_OUT[11], DATA_OUT[12], DATA_OUT[13], DATA_OUT[14], DATA_OUT[15]
  and and_1 (and_1_out, nLB_LOAD, nPC_LOAD);
  and and_2 (nLOW_LOAD, and_1_out, nSTK_LOAD);
  and and_3 (and_3_out, nHB_LOAD, nPC_LOAD);
  and and_4 (nHIGH_LOAD, and_3_out, nSTK_LOAD);

  // Notes on the sheet:
  //   Input from data bus
  //   Input from Program Counter
  //   Input from Stack Pointer
endmodule

module Memory (
  input  BOOT_ROM,
  input  PROGRAM_RAM,
  input  nRAM_LOAD,
  input  nMEM_OUT,
  input  CLOCK,
  input  [15:0] ADDRESS_IN,
  input  [7:0] DATA_IN,
  input  [7:0] MANUAL_DATA_IN,
  output [7:0] CONTENTS_OUT,
  output [7:0] DATA_OUT
);

  wire and_1_out, nMEM_OUT_t, not_2_out, not_3_out, not_4_out, not_5_out, not_6_out, nRAM_CE, nRAM_WE,
       nROM_CE, or_1_out;

  not not_1 (nRAM_CE, nROM_CE);
  or or_1 (or_1_out, ADDRESS_IN[14], ADDRESS_IN[15]);
  nand nand_1 (nROM_CE, or_1_out, BOOT_ROM);
  not not_2 (not_2_out, nRAM_CE);
  not not_3 (not_3_out, CLOCK);
  not not_4 (not_4_out, nROM_CE);
  RAM #(.addrWidth(16)) ram_1 (
    .addr(ADDRESS_IN), .data(CONTENTS_OUT), .sel(not_2_out), .clk(not_3_out), .ld(nRAM_WE), .clr(1'b0));
  ROM #(.addrWidth(16)) rom_1 (.addr(ADDRESS_IN), .data(CONTENTS_OUT), .sel(not_4_out));
  or or_2 (nMEM_OUT_t, PROGRAM_RAM, nMEM_OUT);
  not not_5 (not_5_out, PROGRAM_RAM);
  // IC_74244 ic_74244_1: pin names not known; wires that end beside it: CONTENTS_OUT[0], CONTENTS_OUT[1], CONTENTS_OUT[2], CONTENTS_OUT[3], CONTENTS_OUT[4], CONTENTS_OUT[5], CONTENTS_OUT[6], CONTENTS_OUT[7], DATA_OUT[0], DATA_OUT[1], DATA_OUT[2], DATA_OUT[3], DATA_OUT[4], DATA_OUT[5], DATA_OUT[6], DATA_OUT[7]
  // IC_74244 ic_74244_2: pin names not known; wires that end beside it: nMEM_OUT_t, nMEM_OUT_t, DATA_IN[0], DATA_IN[1], DATA_IN[2], DATA_IN[3], DATA_IN[4], DATA_IN[5], DATA_IN[6], DATA_IN[7], CONTENTS_OUT[0], CONTENTS_OUT[1], CONTENTS_OUT[2], CONTENTS_OUT[3], CONTENTS_OUT[4], CONTENTS_OUT[5], CONTENTS_OUT[6], CONTENTS_OUT[7]
  // IC_74244 ic_74244_3: pin names not known; wires that end beside it: nRAM_LOAD, nRAM_LOAD, MANUAL_DATA_IN[0], MANUAL_DATA_IN[1], MANUAL_DATA_IN[2], MANUAL_DATA_IN[3], MANUAL_DATA_IN[4], MANUAL_DATA_IN[5], MANUAL_DATA_IN[6], MANUAL_DATA_IN[7], not_5_out, not_5_out, CONTENTS_OUT[0], CONTENTS_OUT[1], CONTENTS_OUT[2], CONTENTS_OUT[3], CONTENTS_OUT[4], CONTENTS_OUT[5], CONTENTS_OUT[6], CONTENTS_OUT[7]
  and and_1 (and_1_out, PROGRAM_RAM, CLOCK);
  not not_6 (not_6_out, nRAM_LOAD);
  nor nor_1 (nRAM_WE, and_1_out, not_6_out);

  // Notes on the sheet:
  //   Toggle output/input from/to memory chips
  //   RAM
  //   ROM
  //   contents of rom_1 (hex, n*v repeats v):
  //   ab de 32767*0 bb
  //   RAM write switch
endmodule

module Clock_Divider (
  input  CLOCK,
  output CLOCK_DIV64
);

  wire d_ff_1_q, d_ff_1_qn, d_ff_2_q, d_ff_2_qn, d_ff_3_q, d_ff_3_qn, d_ff_4_q, d_ff_4_qn, d_ff_5_q,
       d_ff_5_qn, d_ff_6_q, d_ff_6_qn, d_ff_7_qn;

  D_Flip_Flop d_ff_1 (.clk(CLOCK), .D(d_ff_1_qn), .Q(d_ff_1_q), .Qn(d_ff_1_qn), .en(1'b1));  // open: preset, reset
  D_Flip_Flop d_ff_2 (.clk(d_ff_1_q), .D(d_ff_2_qn), .Q(d_ff_2_q), .Qn(d_ff_2_qn), .en(1'b1));  // open: preset, reset
  D_Flip_Flop d_ff_3 (.clk(d_ff_2_q), .D(d_ff_3_qn), .Q(d_ff_3_q), .Qn(d_ff_3_qn), .en(1'b1));  // open: preset, reset
  D_Flip_Flop d_ff_4 (.clk(d_ff_3_q), .D(d_ff_4_qn), .Q(d_ff_4_q), .Qn(d_ff_4_qn), .en(1'b1));  // open: preset, reset
  D_Flip_Flop d_ff_5 (.clk(d_ff_4_q), .D(d_ff_5_qn), .Q(d_ff_5_q), .Qn(d_ff_5_qn), .en(1'b1));  // open: preset, reset
  D_Flip_Flop d_ff_6 (.clk(d_ff_5_q), .D(d_ff_6_qn), .Q(d_ff_6_q), .Qn(d_ff_6_qn), .en(1'b1));  // open: preset, reset
  D_Flip_Flop d_ff_7 (
    .clk(d_ff_6_q), .D(d_ff_7_qn), .Q(CLOCK_DIV64), .Qn(d_ff_7_qn), .en(1'b1));  // open: preset, reset
endmodule
