// Logisim project 74xx-Computer.circ as structural Verilog: 15 circuits, main circuit 74xx-Computer
module _74xx_Computer (
  input  [7:0] DATA_BUS__IN,
  input  MEM_BOOT_ROM,
  input  MEM_PROGRAM_RAM,
  input  [7:0] MANUAL_DATA,
  output [7:0] DATA_BUS__OUT,
  output Fc,
  output Fz,
  output Fcmp
);

  wire ALU_M, ALU_S0, ALU_S1, ALU_S2, ALU_S3, ALU_SHR, and_1_out, CLOCK_8X, clock_divider_1_clock_div8,
       CLOCK_HALT, FLAGS_Fc_CLEAR, FLAGS_Fc_LOAD, FLAGS_Fc_SET, FLAGS_Feq_LOAD, FLAGS_Fgt_LOAD,
       FLAGS_Flt_LOAD, FLAGS_Fz_LOAD, lcd_decoder_1_lcd_clock, lcd_decoder_1_reset, MEM_BOOT_ROM_t,
       nA_DATA_LOAD, nA_DATA_OUT, nALU_AX_LOAD, nALU_AY_LOAD, nALU_OUT, nB_DATA_LOAD, nB_DATA_OUT,
       nC_DATA_LOAD, nC_DATA_OUT, nD_DATA_LOAD, nD_DATA_OUT, nIR_LOAD, nMAR_HB_LOAD, nMAR_LB_LOAD, nMAR_ZP,
       nMEM_OUT, nMEM_RAM_LOAD, not_2_out, not_3_out, nOUT1_LOAD, nOUT2_LOAD, nPC_H_LOAD, nPC_H_OUT,
       nPC_L_LOAD, nPC_L_OUT, nPC_MAR_OUT, nSTK_MAR_OUT, nSTK_RESET, Output_tty_clock, Output_tty_write,
       PC_DEC, PC_INC, STK_DEC, STK_INC;
  wire [3:0] ALU_alu_ax_contents, ALU_alu_ax_contents_2, ALU_alu_ay_contents, ALU_alu_ay_contents_2,
       ALU_contents_bus_out, ALU_contents_bus_out_2, Memory_Access_Register_data_out,
       Memory_Access_Register_data_out_2, Memory_Access_Register_data_out_3,
       Memory_Access_Register_data_out_4, Memory_contents_out, Memory_contents_out_2,
       Program_Counter_pc_contents, Program_Counter_pc_contents_2, Program_Counter_pc_contents_3,
       Program_Counter_pc_contents_4, Register_A_contents_bus_out, Register_A_contents_bus_out_2,
       Register_B_contents_bus_out, Register_B_contents_bus_out_2, Register_C_contents_bus_out,
       Register_C_contents_bus_out_2, Register_D_contents_bus_out, Register_D_contents_bus_out_2;
  wire [4:0] ALU_fc;
  wire [6:0] lcd_decoder_1_x_coord, lcd_decoder_1_y_coord, Output_tty_data;
  wire [7:0] Instruction_Register_contents_bus_out, Output_contents_bus_out;
  wire [15:0] lcd_decoder_1_color, Program_Counter_mar_bus_out, Stack_Pointer_stk_contents;

  Clock clock_1 (.out(CLOCK_8X));
  not not_1 (MEM_BOOT_ROM_t, MEM_BOOT_ROM);
  Hex_Digit_Display hex_digit_display_1 (.value(DATA_BUS__IN[7:4]));  // open: dp
  Hex_Digit_Display hex_digit_display_2 (.value(DATA_BUS__IN[3:0]));  // open: dp
  Hex_Digit_Display hex_digit_display_3 (.value(Program_Counter_pc_contents_3));  // open: dp
  Hex_Digit_Display hex_digit_display_4 (.value(Program_Counter_pc_contents_4));  // open: dp
  not not_2 (not_2_out, CLOCK_HALT);
  Clock_Divider clock_divider_1 (.CLOCK(CLOCK_8X), .CLOCK_DIV8(clock_divider_1_clock_div8));  // open: CLOCK_DIV64
  Hex_Digit_Display hex_digit_display_5 (.value(Register_C_contents_bus_out));  // open: dp
  Hex_Digit_Display hex_digit_display_6 (.value(Register_C_contents_bus_out_2));  // open: dp
  Register Register_C (
    .CLOCK(and_1_out), .nDATA_OUT(nC_DATA_OUT), .nDATA_LOAD(nC_DATA_LOAD),
    .CONTENTS_BUS_OUT({Register_C_contents_bus_out_2, Register_C_contents_bus_out}),
    .DATA_BUS_OUT(DATA_BUS__IN), .DATA_BUS_IN(DATA_BUS__IN));
  Hex_Digit_Display hex_digit_display_7 (.value(Program_Counter_pc_contents));  // open: dp
  Hex_Digit_Display hex_digit_display_8 (.value(Program_Counter_pc_contents_2));  // open: dp
  Hex_Digit_Display hex_digit_display_9 (.value(Register_D_contents_bus_out_2));  // open: dp
  Hex_Digit_Display hex_digit_display_10 (.value(Register_D_contents_bus_out));  // open: dp
  Register Register_D (
    .CLOCK(and_1_out), .nDATA_OUT(nD_DATA_OUT), .nDATA_LOAD(nD_DATA_LOAD),
    .CONTENTS_BUS_OUT({Register_D_contents_bus_out_2, Register_D_contents_bus_out}),
    .DATA_BUS_OUT(DATA_BUS__IN), .DATA_BUS_IN(DATA_BUS__IN));
  Hex_Digit_Display hex_digit_display_11 (.value(Register_A_contents_bus_out));  // open: dp
  Hex_Digit_Display hex_digit_display_12 (.value(Register_A_contents_bus_out_2));  // open: dp
  Register Register_A (
    .CLOCK(and_1_out), .nDATA_OUT(nA_DATA_OUT), .nDATA_LOAD(nA_DATA_LOAD),
    .CONTENTS_BUS_OUT({Register_A_contents_bus_out_2, Register_A_contents_bus_out}),
    .DATA_BUS_OUT(DATA_BUS__IN), .DATA_BUS_IN(DATA_BUS__IN));
  Hex_Digit_Display hex_digit_display_13 (.value(Register_B_contents_bus_out));  // open: dp
  Hex_Digit_Display hex_digit_display_14 (.value(Register_B_contents_bus_out_2));  // open: dp
  Register Register_B (
    .CLOCK(and_1_out), .nDATA_OUT(nB_DATA_OUT), .nDATA_LOAD(nB_DATA_LOAD),
    .CONTENTS_BUS_OUT({Register_B_contents_bus_out_2, Register_B_contents_bus_out}),
    .DATA_BUS_OUT(DATA_BUS__IN), .DATA_BUS_IN(DATA_BUS__IN));
  and and_1 (and_1_out, not_2_out, clock_divider_1_clock_div8);
  Program_Counter Program_Counter (
    .PC_INC(PC_INC), .PC_DEC(PC_DEC), .CLOCK(and_1_out), .PC_L_DATA_IN(DATA_BUS__IN),
    .nPC_L_LOAD(nPC_L_LOAD), .PC_H_DATA_IN(DATA_BUS__IN), .nPC_H_LOAD(nPC_H_LOAD), .nPC_L_OUT(nPC_L_OUT),
    .PC_L_DATA_OUT(DATA_BUS__IN), .PC_H_DATA_OUT(DATA_BUS__IN), .nPC_H_OUT(nPC_H_OUT),
    .nPC_MAR_OUT(nPC_MAR_OUT), .MAR_BUS_OUT(Program_Counter_mar_bus_out),
    .PC_CONTENTS({Program_Counter_pc_contents_4, Program_Counter_pc_contents_3, Program_Counter_pc_contents_2, Program_Counter_pc_contents}));
  not not_3 (not_3_out, Fc);
  Hex_Digit_Display hex_digit_display_15 (.value(ALU_alu_ax_contents_2));  // open: dp
  Hex_Digit_Display hex_digit_display_16 (.value(ALU_alu_ax_contents));  // open: dp
  Flags_Register Flags_Register (
    .CLOCK(and_1_out), .Fgt_IN(ALU_fc[4]), .Fz_IN(ALU_fc[1]), .Fgt_LOAD(FLAGS_Fgt_LOAD),
    .Fz_LOAD(FLAGS_Fz_LOAD), .Fcmp_OUT(Fcmp), .Flt_IN(ALU_fc[2]), .Fz_OUT(Fz), .Flt_LOAD(FLAGS_Flt_LOAD),
    .Fc_CLEAR(FLAGS_Fc_CLEAR), .Feq_IN(ALU_fc[3]), .Feq_LOAD(FLAGS_Feq_LOAD), .Fc_LOAD(FLAGS_Fc_LOAD),
    .Fc_OUT(Fc), .Fc_IN(ALU_fc[0]), .Fc_SET(FLAGS_Fc_SET));
  Hex_Digit_Display hex_digit_display_17 (.value(ALU_alu_ay_contents));  // open: dp
  Hex_Digit_Display hex_digit_display_18 (.value(ALU_alu_ay_contents_2));  // open: dp
  Hex_Digit_Display hex_digit_display_19 (.value(Stack_Pointer_stk_contents[15:12]));  // open: dp
  Stack_Pointer Stack_Pointer (
    .STK_DEC(STK_DEC), .CLOCK(and_1_out), .nSTK_RESET(nSTK_RESET), .STK_INC(STK_INC),
    .nSTK_OUT(nSTK_MAR_OUT), .STK_CONTENTS(Stack_Pointer_stk_contents),
    .MAR_BUS_OUT(Program_Counter_mar_bus_out));
  Hex_Digit_Display hex_digit_display_20 (.value(Memory_Access_Register_data_out_4));  // open: dp
  Memory_Access_Register Memory_Access_Register (
    .LB_DATA_IN(DATA_BUS__IN), .CLOCK(and_1_out), .nLB_LOAD(nMAR_LB_LOAD), .HB_DATA_IN(DATA_BUS__IN),
    .nHB_LOAD(nMAR_HB_LOAD), .DATA_IN(Program_Counter_mar_bus_out),
    .DATA_OUT({Memory_Access_Register_data_out_4, Memory_Access_Register_data_out_3, Memory_Access_Register_data_out_2, Memory_Access_Register_data_out}),
    .nZP_LOAD(nMAR_ZP), .nPC_MAR_OUT(nSTK_MAR_OUT), .nSTK_MAR_OUT(nPC_MAR_OUT));
  ALU ALU (
    .DATA_BUS_IN(DATA_BUS__IN), .CLOCK(and_1_out), .nAX_IN(nALU_AX_LOAD), .nAY_IN(nALU_AY_LOAD), .S3(ALU_S3),
    .S2(ALU_S2), .S1(ALU_S1), .S0(ALU_S0), .M(ALU_M), .Cn(not_3_out), .nALU_OUT(nALU_OUT), .Flt(ALU_fc[2]),
    .Feq(ALU_fc[3]), .Fgt(ALU_fc[4]), .DATA_BUS_OUT(DATA_BUS__IN),
    .CONTENTS_BUS_OUT({ALU_contents_bus_out_2, ALU_contents_bus_out}),
    .ALU_AX_CONTENTS({ALU_alu_ax_contents_2, ALU_alu_ax_contents}),
    .ALU_AY_CONTENTS({ALU_alu_ay_contents_2, ALU_alu_ay_contents}), .SHR(ALU_SHR), .Fc(ALU_fc[0]),
    .Fz(ALU_fc[1]));
  Hex_Digit_Display hex_digit_display_21 (.value(Stack_Pointer_stk_contents[11:8]));  // open: dp
  Hex_Digit_Display hex_digit_display_22 (.value(Stack_Pointer_stk_contents[7:4]));  // open: dp
  Hex_Digit_Display hex_digit_display_23 (.value(Memory_Access_Register_data_out_2));  // open: dp
  Hex_Digit_Display hex_digit_display_24 (.value(Memory_Access_Register_data_out_3));  // open: dp
  Hex_Digit_Display hex_digit_display_25 (.value(ALU_contents_bus_out_2));  // open: dp
  Hex_Digit_Display hex_digit_display_26 (.value(ALU_contents_bus_out));  // open: dp
  Hex_Digit_Display hex_digit_display_27 (.value(Stack_Pointer_stk_contents[3:0]));  // open: dp
  Hex_Digit_Display hex_digit_display_28 (.value(Memory_Access_Register_data_out));  // open: dp
  Hex_Digit_Display hex_digit_display_29 (.value(Instruction_Register_contents_bus_out[7:4]));  // open: dp
  Hex_Digit_Display hex_digit_display_30 (.value(Instruction_Register_contents_bus_out[3:0]));  // open: dp
  Register Instruction_Register (
    .CLOCK(and_1_out), .nDATA_OUT(1'b0), .nDATA_LOAD(nIR_LOAD),
    .CONTENTS_BUS_OUT(Instruction_Register_contents_bus_out), .DATA_BUS_IN(DATA_BUS__IN));  // open: DATA_BUS_OUT
  Hex_Digit_Display hex_digit_display_31 (.value(Output_contents_bus_out[7:4]));  // open: dp
  Output_Control Output (
    .DATA_BUS_IN(DATA_BUS__IN), .CLOCK(and_1_out), .nOUT1_LOAD(nOUT1_LOAD),
    .CONTENTS_BUS_OUT(Output_contents_bus_out), .TTY_WRITE(Output_tty_write), .TTY_DATA(Output_tty_data),
    .TTY_CLOCK(Output_tty_clock), .CLOCK_8X(CLOCK_8X));  // open: nOUT2_LOAD
  Hex_Digit_Display hex_digit_display_32 (.value(Memory_contents_out_2));  // open: dp
  Memory Memory (
    .BOOT_ROM(MEM_BOOT_ROM_t), .PROGRAM_RAM(MEM_PROGRAM_RAM), .nRAM_LOAD(nMEM_RAM_LOAD), .nMEM_OUT(nMEM_OUT),
    .CLOCK(and_1_out), .DATA_IN(DATA_BUS__IN), .MANUAL_DATA_IN(MANUAL_DATA), .DATA_OUT(DATA_BUS__IN),
    .ADDRESS_IN({Memory_Access_Register_data_out_4, Memory_Access_Register_data_out_3, Memory_Access_Register_data_out_2, Memory_Access_Register_data_out}),
    .CONTENTS_OUT({Memory_contents_out_2, Memory_contents_out}));
  Hex_Digit_Display hex_digit_display_33 (.value(Output_contents_bus_out[3:0]));  // open: dp
  Hex_Digit_Display hex_digit_display_34 (.value(Memory_contents_out));  // open: dp
  Controller Controller (
    .nA_DATA_OUT(nA_DATA_OUT), .nSTK_RESET(nSTK_RESET), .nA_DATA_LOAD(nA_DATA_LOAD),
    .nALU_AX_LOAD(nALU_AX_LOAD), .nB_DATA_OUT(nB_DATA_OUT), .nALU_AY_LOAD(nALU_AY_LOAD),
    .FLAGS_DATA_IN({Fcmp, Fz, Fc}), .nB_DATA_LOAD(nB_DATA_LOAD), .ALU_S0(ALU_S0),
    .INSTRUCTION_DATA_IN(Instruction_Register_contents_bus_out), .nC_DATA_OUT(nC_DATA_OUT), .ALU_S1(ALU_S1),
    .nC_DATA_LOAD(nC_DATA_LOAD), .ALU_S2(ALU_S2), .nD_DATA_OUT(nD_DATA_OUT), .ALU_S3(ALU_S3),
    .CLOCK(and_1_out), .nD_DATA_LOAD(nD_DATA_LOAD), .ALU_M(ALU_M), .CLOCK_8X(CLOCK_8X),
    .FLAGS_Fz_LOAD(FLAGS_Fz_LOAD), .ALU_SHR(ALU_SHR), .nIR_LOAD(nIR_LOAD), .nALU_OUT(nALU_OUT),
    .nMAR_LB_LOAD(nMAR_LB_LOAD), .PC_INC(PC_INC), .nMAR_HB_LOAD(nMAR_HB_LOAD), .nPC_MAR_OUT(nPC_MAR_OUT),
    .PC_DEC(PC_DEC), .nSTK_MAR_OUT(nSTK_MAR_OUT), .nPC_L_LOAD(nPC_L_LOAD), .nMEM_RAM_LOAD(nMEM_RAM_LOAD),
    .nPC_H_LOAD(nPC_H_LOAD), .nMEM_OUT(nMEM_OUT), .nPC_L_OUT(nPC_L_OUT), .nPC_H_OUT(nPC_H_OUT),
    .CLOCK_HALT(CLOCK_HALT), .STK_INC(STK_INC), .STK_DEC(STK_DEC), .FLAGS_Fc_LOAD(FLAGS_Fc_LOAD),
    .FLAGS_Flt_LOAD(FLAGS_Flt_LOAD), .FLAGS_Feq_LOAD(FLAGS_Feq_LOAD), .FLAGS_Fgt_LOAD(FLAGS_Fgt_LOAD),
    .FLAGS_Fc_CLEAR(FLAGS_Fc_CLEAR), .FLAGS_Fc_SET(FLAGS_Fc_SET), .nOUT1_LOAD(nOUT1_LOAD), .nMAR_ZP(nMAR_ZP),
    .nOUT2_LOAD(nOUT2_LOAD));
  TTY tty_1 (.data(Output_tty_data), .clk(Output_tty_clock), .we(Output_tty_write), .clr(1'b0));
  LCD_Decoder lcd_decoder_1 (
    .DATA(DATA_BUS__IN), .CLOCK(and_1_out), .nLOAD(nOUT2_LOAD), .RESET(lcd_decoder_1_reset),
    .LCD_CLOCK(lcd_decoder_1_lcd_clock), .COLOR(lcd_decoder_1_color), .X_COORD(lcd_decoder_1_x_coord),
    .Y_COORD(lcd_decoder_1_y_coord));
  // LCD_Video lcd_video_1: pin names not known; wires that end beside it: lcd_decoder_1_reset, lcd_decoder_1_lcd_clock, 1'b1, lcd_decoder_1_x_coord, lcd_decoder_1_y_coord, lcd_decoder_1_color

  assign DATA_BUS__OUT = DATA_BUS__IN;

  // Other names for the same wires on the sheet: FLAGS_Fc = Fc

  // Notes on the sheet:
  //   AX Register
  //   AY Register
  //   ALU Result
endmodule

module Controller (
  input  [2:0] FLAGS_DATA_IN,
  input  [7:0] INSTRUCTION_DATA_IN,
  input  CLOCK,
  input  CLOCK_8X,
  output nA_DATA_OUT,
  output nSTK_RESET,
  output nA_DATA_LOAD,
  output nALU_AX_LOAD,
  output nB_DATA_OUT,
  output nALU_AY_LOAD,
  output nB_DATA_LOAD,
  output ALU_S0,
  output nC_DATA_OUT,
  output ALU_S1,
  output nC_DATA_LOAD,
  output ALU_S2,
  output nD_DATA_OUT,
  output ALU_S3,
  output nD_DATA_LOAD,
  output ALU_M,
  output FLAGS_Fz_LOAD,
  output ALU_SHR,
  output nIR_LOAD,
  output nALU_OUT,
  output nMAR_LB_LOAD,
  output PC_INC,
  output nMAR_HB_LOAD,
  output nPC_MAR_OUT,
  output PC_DEC,
  output nSTK_MAR_OUT,
  output nPC_L_LOAD,
  output nMEM_RAM_LOAD,
  output nPC_H_LOAD,
  output nMEM_OUT,
  output nPC_L_OUT,
  output nPC_H_OUT,
  output CLOCK_HALT,
  output STK_INC,
  output FLAGS_Fc_LOAD,
  output STK_DEC,
  output FLAGS_Flt_LOAD,
  output FLAGS_Feq_LOAD,
  output FLAGS_Fgt_LOAD,
  output FLAGS_Fc_CLEAR,
  output FLAGS_Fc_SET,
  output nOUT1_LOAD,
  output nOUT2_LOAD,
  output nMAR_ZP
);

  wire A_DATA_LOAD, A_DATA_OUT, ALU_AX_LOAD, ALU_AY_LOAD, ALU_OUT, and_1_out, and_2_out, and_4_out,
       B_DATA_LOAD, B_DATA_OUT, C_DATA_LOAD, C_DATA_OUT, CLOCK_8X_out, D_DATA_LOAD, D_DATA_OUT,
       dip_7474_1_p1, dip_7474_2_p1, dip_7474_2_p2, dip_7474_2_p3, dip_7474_2_p4, dip_74138_1_p2,
       dip_74138_1_p4, dip_74138_1_p6, dip_74138_1_p7, dip_74138_1_p8, dip_74138_1_p10, dip_74138_1_p12,
       dip_74161_1_p1, ic_74273_2_p1, ic_74273_4_p1, ic_74273_6_p4, IN_OUT, IR_LOAD, MAR_HB_LOAD,
       MAR_LB_LOAD, MAR_ZP, MEM_OUT, MEM_RAM_LOAD, n74161_clockfix_3_tc, nLOAD_DONE, nor_2_out, nor_4_out,
       nor_6_out, nor_7_out, not_1_out, not_2_out, not_3_out, not_4_out, not_6_out, or_1_out, or_2_out,
       or_4_out, or_5_out, OUT1_LOAD, OUT2_LOAD, PC_H_LOAD, PC_H_OUT, PC_INC_t, PC_L_LOAD, PC_L_OUT,
       PC_MAR_OUT, ROM_ENABLE, RUNNING, STK_MAR_OUT, STK_RESET, TSTATE_0, TSTATE_1, TSTATE_RESET;
  wire [2:0] BANK;
  wire [3:2] undriven;
  wire [4:0] T_STATE;
  wire [7:0] ROM_DATA;

  not not_1 (not_1_out, RUNNING);
  // Probe on FLAGS_DATA_IN[2]
  Clock u_CLOCK_8X (.out(CLOCK_8X_out));
  Clock_Divider clock_divider_1 (.CLOCK(CLOCK_8X_out));  // open: CLOCK_DIV8, CLOCK_DIV64
  and and_1 (and_1_out, not_1_out, CLOCK);
  _74161_Clockfix u_74161_clockfix_1 (
    .CLK(CLOCK), .CLR(not_3_out), .LE(1'b1), .CEP(n74161_clockfix_3_tc), .CET(n74161_clockfix_3_tc),
    .D1(1'b0), .D2(1'b0), .D3(1'b0), .D4(1'b0), .Q1(T_STATE[4]));  // open: Q2, Q3, Q4, TC
  not not_2 (not_2_out, RUNNING);
  or or_1 (or_1_out, not_2_out, TSTATE_RESET);
  // Probe on FLAGS_DATA_IN[1]
  // Probe on FLAGS_DATA_IN[0]
  _74161_Clockfix u_74161_clockfix_2 (
    .CLK(and_1_out), .CLR(1'b1), .LE(1'b1), .CEP(1'b1), .CET(1'b1), .D1(1'b0), .D2(1'b0), .D3(1'b0),
    .D4(1'b0), .Q2(RUNNING));  // open: Q1, Q3, Q4, TC
  DotMatrix #(.matrixrows(1), .dotshape("circle")) dotmatrix_1 (
    .col0(T_STATE[4]), .col1(T_STATE[3]), .col2(T_STATE[2]), .col3(T_STATE[1]), .col4(T_STATE[0]));
  _74161_Clockfix u_74161_clockfix_3 (
    .CLK(CLOCK), .CLR(not_3_out), .LE(1'b1), .CEP(1'b1), .CET(1'b1), .D1(1'b0), .D2(1'b0), .D3(1'b0),
    .D4(1'b0), .Q1(T_STATE[0]), .Q2(T_STATE[1]), .Q3(T_STATE[2]), .Q4(T_STATE[3]), .TC(n74161_clockfix_3_tc));
  not not_3 (not_3_out, and_2_out);
  and and_2 (and_2_out, or_1_out, not_4_out);
  not not_4 (not_4_out, CLOCK);
  // Probe on INSTRUCTION_DATA_IN[7]
  // Probe on INSTRUCTION_DATA_IN[6]
  // Probe on INSTRUCTION_DATA_IN[5]
  // Probe on INSTRUCTION_DATA_IN[4]
  // Probe on INSTRUCTION_DATA_IN[3]
  // Probe on INSTRUCTION_DATA_IN[2]
  ROM #(.addrWidth(19)) rom_1 (.addr({FLAGS_DATA_IN, INSTRUCTION_DATA_IN, T_STATE, BANK}), .data(ROM_DATA), .sel(1'b1));
  // Probe on INSTRUCTION_DATA_IN[1]
  // Probe on INSTRUCTION_DATA_IN[0]
  nor nor_1 (TSTATE_0, T_STATE[0], T_STATE[1], T_STATE[2], T_STATE[3], T_STATE[4]);
  // Probe on T_STATE[3]
  // Probe on T_STATE[4]
  // Probe on T_STATE[2]
  // DIP_7474 dip_7474_1: pin names not known; wires that end beside it: dip_7474_1_p1, 1'b1, 1'b1, dip_7474_1_p1, ROM_ENABLE
  and and_3 (TSTATE_1, T_STATE[0], nor_2_out);
  nor nor_2 (nor_2_out, T_STATE[1], T_STATE[2], T_STATE[3], T_STATE[4]);
  // Probe on T_STATE[0]
  // Probe on T_STATE[1]
  // IC_74273 ic_74273_1: pin names not known
  not not_5 (nLOAD_DONE, dip_7474_2_p4);
  Hex_Digit_Display hex_digit_display_1 (.value({undriven, FLAGS_Fc_SET, FLAGS_Fc_CLEAR}));  // open: dp
  Hex_Digit_Display hex_digit_display_2 (.value({FLAGS_Fc_LOAD, FLAGS_Flt_LOAD, FLAGS_Feq_LOAD, FLAGS_Fgt_LOAD}));  // open: dp
  not not_6 (not_6_out, and_4_out);
  and and_4 (and_4_out, CLOCK_8X, nLOAD_DONE);
  // DIP_7474 dip_7474_2: pin names not known; wires that end beside it: dip_7474_2_p1, dip_7474_2_p2, dip_7474_2_p3, dip_7474_2_p4
  not not_7 (dip_7474_2_p1, CLOCK);
  and and_5 (dip_7474_2_p3, CLOCK_8X, nLOAD_DONE);
  Hex_Digit_Display hex_digit_display_3 (.value({TSTATE_RESET, CLOCK_HALT, MEM_OUT, MEM_RAM_LOAD}));  // open: dp
  Hex_Digit_Display hex_digit_display_4 (.value({FLAGS_Fz_LOAD, OUT2_LOAD, OUT1_LOAD, IN_OUT}));  // open: dp
  // IC_74273 ic_74273_2: pin names not known; wires that end beside it: ic_74273_2_p1, RUNNING
  nor nor_3 (ic_74273_2_p1, not_6_out, dip_74138_1_p2);
  // IC_74273 ic_74273_3: pin names not known
  Hex_Digit_Display hex_digit_display_5 (.value({ALU_SHR, ALU_M, ALU_S3, ALU_S2}));  // open: dp
  Hex_Digit_Display hex_digit_display_6 (.value({MAR_ZP, MAR_HB_LOAD, MAR_LB_LOAD, ALU_OUT}));  // open: dp
  nor nor_4 (nor_4_out, not_6_out, dip_74138_1_p6);
  // IC_74273 ic_74273_4: pin names not known; wires that end beside it: ic_74273_4_p1, RUNNING
  nor nor_5 (ic_74273_4_p1, not_6_out, dip_74138_1_p4);
  Hex_Digit_Display hex_digit_display_7 (.value({STK_MAR_OUT, STK_RESET, STK_DEC, STK_INC}));  // open: dp
  Hex_Digit_Display hex_digit_display_8 (.value({ALU_S1, ALU_S0, ALU_AY_LOAD, ALU_AX_LOAD}));  // open: dp
  // IC_74273 ic_74273_5: pin names not known; wires that end beside it: nor_4_out, RUNNING, RUNNING
  nor nor_6 (nor_6_out, not_6_out, dip_74138_1_p8);
  and and_6 (dip_7474_2_p2, BANK[2], BANK[1], BANK[0]);
  Hex_Digit_Display hex_digit_display_9 (.value({PC_DEC, PC_INC_t, PC_MAR_OUT, IR_LOAD}));  // open: dp
  Hex_Digit_Display hex_digit_display_10 (.value({PC_H_OUT, PC_L_OUT, PC_H_LOAD, PC_L_LOAD}));  // open: dp
  nor nor_7 (nor_7_out, not_6_out, dip_74138_1_p10);
  // IC_74273 ic_74273_6: pin names not known; wires that end beside it: nor_6_out, RUNNING, nor_7_out, ic_74273_6_p4, RUNNING
  // DIP_74161 dip_74161_1: pin names not known; wires that end beside it: dip_74161_1_p1, CLOCK_8X, BANK[0], 1'b0, BANK[1], 1'b0, BANK[2], 1'b0, 1'b0, 1'b1, 1'b1, 1'b1
  and and_7 (dip_74161_1_p1, RUNNING, nLOAD_DONE);
  Hex_Digit_Display hex_digit_display_11 (.value({B_DATA_LOAD, B_DATA_OUT, A_DATA_LOAD, A_DATA_OUT}));  // open: dp
  Hex_Digit_Display hex_digit_display_12 (.value({D_DATA_LOAD, D_DATA_OUT, C_DATA_LOAD, C_DATA_OUT}));  // open: dp
  nor nor_8 (ic_74273_6_p4, not_6_out, dip_74138_1_p12);
  // DIP_74138 dip_74138_1: pin names not known; wires that end beside it: BANK[0], dip_74138_1_p2, BANK[1], dip_74138_1_p4, BANK[2], dip_74138_1_p6, dip_74138_1_p7, dip_74138_1_p8, dip_74138_1_p7, dip_74138_1_p10, 1'b1, dip_74138_1_p12
  not not_8 (dip_74138_1_p7, 1'b1);
  not not_9 (nA_DATA_OUT, A_DATA_OUT);
  not not_10 (nA_DATA_LOAD, A_DATA_LOAD);
  not not_11 (nB_DATA_OUT, B_DATA_OUT);
  not not_12 (nB_DATA_LOAD, B_DATA_LOAD);
  not not_13 (nC_DATA_OUT, C_DATA_OUT);
  not not_14 (nC_DATA_LOAD, C_DATA_LOAD);
  not not_15 (nD_DATA_OUT, D_DATA_OUT);
  not not_16 (nD_DATA_LOAD, D_DATA_LOAD);
  not not_17 (nIR_LOAD, or_2_out);
  not not_18 (nPC_L_LOAD, PC_L_LOAD);
  not not_19 (nPC_H_LOAD, PC_H_LOAD);
  not not_20 (nPC_L_OUT, PC_L_OUT);
  not not_21 (nPC_H_OUT, PC_H_OUT);
  or or_2 (or_2_out, IR_LOAD, TSTATE_1);
  or or_3 (PC_INC, PC_INC_t, TSTATE_1);
  not not_22 (nSTK_RESET, STK_RESET);
  not not_23 (nALU_AX_LOAD, ALU_AX_LOAD);
  not not_24 (nALU_AY_LOAD, ALU_AY_LOAD);
  not not_25 (nALU_OUT, ALU_OUT);
  not not_26 (nMAR_LB_LOAD, MAR_LB_LOAD);
  not not_27 (nMAR_HB_LOAD, MAR_HB_LOAD);
  not not_28 (nPC_MAR_OUT, or_4_out);
  not not_29 (nSTK_MAR_OUT, STK_MAR_OUT);
  not not_30 (nMEM_RAM_LOAD, MEM_RAM_LOAD);
  not not_31 (nMEM_OUT, or_5_out);
  not not_32 (nOUT1_LOAD, OUT1_LOAD);
  not not_33 (nOUT2_LOAD, OUT2_LOAD);
  not not_34 (nMAR_ZP, MAR_ZP);
  or or_4 (or_4_out, PC_MAR_OUT, TSTATE_0);
  or or_5 (or_5_out, MEM_OUT, TSTATE_1);

  // Other names for the same wires on the sheet: FLAGS[2:0] = FLAGS_DATA_IN; INSTRUCTION[7:0] = INSTRUCTION_DATA_IN

  // Notes on the sheet:
  //   Power-up delay:. Start controller after 2 clock cycles
  //   T-STATE COUNTER
  //   CONTROL ROM
  //   contents of rom_1 (hex, n*v repeats v):
  //   17*0 8 255*0 4 259*0 9 0 0 0 8 251*0 21 0 0 0 8 251*0 81 0 0 0 8 251*0 6 0 0 0 8 251*0 24 0 0 0 8
  //   251*0 84 0 0 0 8 251*0 12 0 0 0 8 251*0 18 0 0 0 8 251*0 90 0 0 0 8 251*0 42 0 0 0 8 251*0 48 0 0 0
  //   8 251*0 60 0 0 0 8 250*0 2 4*0 2 0 0 4 2 0 0 0 8 242*0 2 4*0 2 0 0 4 8 0 0 0 8 242*0 2 4*0 2 0 0 4
  //   20 0 0 0 8 242*0 2 4*0 2 0 0 4 80 0 0 0 8 242*0 2 4*0 2 0 0 4 80 6*0 2 4*0 2 0 0 4 20 4*0 20 0 0 10
  //   4*0 40 0 0 40 0 0 0 2 0 0 0 2 0 0 0 8 202*0 2 4*0 2 0 0 4 80 6*0 2 4*0 2 0 0 4 20 4*0 20 0 0 10 4*0
  //   40 0 0 40 0 0 0 2 0 0 0 8 0 0 0 8 198*0 10 0 13 0 0 2 0 0 0 8 246*0 10 0 13 0 0 8 0 0 0 8 250*0 2
  //   4*0 2 0 0 4 80 6*0 2 4*0 2 0 0 4 20 4*0 20 0 0 10 4*0 40 0 0 40 0 0 0 1 0 0 0 1 0 0 0 8 202*0 2 4*0
  //   2 0 0 4 80 6*0 2 4*0 2 0 0 4 20 4*0 20 0 0 10 4*0 40 0 0 40 0 0 0 1 0 0 0 4 0 0 0 8 198*0 10 0 13 0
  //   0 20 0 0 0 8 246*0 10 0 13 0 0 80 0 0 0 8 246*0 10 9*0 12 40 0 2 0 0 8 80 2 40 5*0 8 230*0 10 9*0 12
  //   40 0 20 0 0 8 80 2 40 5*0 8 230*0 10 9*0 12 40 0 80 0 0 8 80 2 40 5*0 8 232*0 12 40 0 2 0 0 8 80 2
  //   40 5*0 8 240*0 12 40 0 20 0 0 8 80 2 40 5*0 8 240*0 12 40 0 80 0 0 8 80 2 40 5*0 8 238*0 20 9*0 11
  //   80 0 2 0 0 8 80 1 80 5*0 8 230*0 20 9*0 11 80 0 20 0 0 8 80 1 80 5*0 8 230*0 20 9*0 11 80 0 80 0 0 8
  //   80 1 80 5*0 8 232*0 11 80 0 2 0 0 8 80 1 80 5*0 8 240*0 11 80 0 20 0 0 8 80 1 80 5*0 8 240*0 11 80 0
  //   80 0 0 8 80 1 80 5*0 8 240*0 16 c0 0 2 0 0 0 8 248*0 16 c0 0 20 0 0 0 8 248*0 16 c0 0 80 0 0 0 8
  //   246*0 10 0 10 40 0 2 0 0 0 8 246*0 10 0 10 40 0 20 0 0 0 8 246*0 10 0 10 40 0 80 0 0 0 8 246*0 10 0
  //   15 80 0 2 0 0 0 8 246*0 10 0 15 80 0 8 0 0 0 8 246*0 10 0 15 80 0 20 0 0 0 8 246*0 10 0 15 80 0 80 0
  //   0 0 8 248*0 14 0 0 2 0 0 0 8 248*0 14 0 0 8 0 0 0 8 248*0 14 0 0 20 0 0 0 8 248*0 14 0 0 80 0 0 0 8
  //   246*0 20 9*0 10 0 0 2 0 0 8 80 7*0 8 230*0 20 9*0 10 0 0 8 0 0 8 80 7*0 8 230*0 20 9*0 10 0 0 20 0 0
  //   8 80 7*0 8 230*0 20 9*0 10 0 0 80 0 0 8 80 7*0 8 230*0 18 80 13 c0 0 2 0 0 8 80 3 c0 5*0 8 238*0 18
  //   80 13 c0 0 8 0 0 8 80 3 c0 5*0 8 238*0 18 80 13 c0 0 20 0 0 8 80 3 c0 5*0 8 238*0 18 80 13 c0 0 80 0
  //   0 8 80 3 c0 5*0 8 238*0 12 0 1 80 5*0 8 250*0 2 4*0 2 0 10 4 4*0 8 242*0 2 4*0 2 0 20 4 4*0 8 242*0
  //   2 4*0 2 0 0 4 80 6*0 2 4*0 2 0 0 0 20 6*0 10 10 6*0 20 40 0 0 0 8 210*0 4 7*0 4 4*0 8 7*0 2 0 0 4 20
  //   6*0 10 10 6*0 20 40 0 0 0 8 210*0 2 4*0 2 0 0 4 80 6*0 2 4*0 2 0 0 4 20 6*0 10 10 6*0 20 40 0 0 0 8
  //   210*0 4 7*0 4 4*0 8 7*0 2 0 0 4 20 6*0 10 10 6*0 20 40 0 0 0 8 210*0 2 4*0 2 0 0 4 80 6*0 2 4*0 2 0
  //   0 4 20 6*0 10 10 6*0 20 40 0 0 0 8 210*0 4 7*0 4 4*0 8 7*0 2 0 0 4 20 6*0 10 10 6*0 20 40 0 0 0 8
  //   210*0 2 4*0 2 0 0 4 80 6*0 2 4*0 2 0 0 4 20 6*0 10 10 6*0 20 40 0 0 0 8 466*0 4 7*0 4 7*0 40 20 6*0
  //   80 80 5*0 8 5*0 1 0 1 8 40 5*0 8 5*0 1 0 1 8 10 6*0 2 4*0 2 0 0 4 80 6*0 2 4*0 2 0 0 4 20 6*0 20 40
  //   6*0 10 10 149*0 2 7*0 8 5*0 2 0 2 0 20 5*0 8 5*0 2 0 0 0 80 6*0 10 10 6*0 20 40 0 0 0 8 1223*0 20 0
  //   0 0 1 0 0 0 8 247*0 20 0 0 0 4 0 0 0 8 247*0 20 0 0 0 10 0 0 0 8 247*0 20 0 0 0 40 0 0 0 8 247*0 40
  //   0 0 0 1 0 0 0 8 247*0 40 0 0 0 4 0 0 0 8 247*0 40 0 0 0 10 0 0 0 8 247*0 40 0 0 0 40 0 0 0 8 249*0
  //   10 0 1 0 0 0 8 249*0 10 0 4 0 0 0 8 249*0 10 0 10 0 0 0 8 249*0 10 0 40 0 0 0 8 249*0 20 0 1 0 0 0 8
  //   249*0 20 0 4 0 0 0 8 249*0 20 0 10 0 0 0 8 249*0 20 0 40 0 0 0 8 246*0 8 80 8 0 0 2 0 0 0 8 246*0 8
  //   80 8 0 0 8 0 0 0 8 246*0 8 80 8 0 0 20 0 0 0 8 250*0 2 4*0 2 0 0 4 20 4*0 a0 0 0 10 0 0 0 1 0 0 0 1
  //   0 0 0 8 222*0 10 9*0 12 40 0 8 0 0 8 80 2 40 5*0 8 232*0 12 40 0 8 0 0 8 80 2 40 5*0 8 238*0 20 9*0
  //   11 80 0 8 0 0 8 80 1 80 5*0 8 232*0 11 80 0 8 0 0 8 80 1 80 5*0 8 240*0 16 c0 0 8 0 0 0 8 246*0 10 0
  //   10 40 0 8 0 0 0 8 246*0 8 80 8 0 0 80 0 0 0 8 246*0 10 8*0 8 246*0 20 8*0 8 250*0 2 4*0 2 0 0 4 80
  //   6*0 2 4*0 2 0 0 4 20 4*0 20 0 0 10 4*0 40 0 0 40 0 0 0 2 0 10 5*0 8 202*0 2 4*0 2 0 0 4 80 6*0 2 4*0
  //   2 0 0 4 20 4*0 20 0 0 10 4*0 40 0 0 40 0 0 0 2 0 20 5*0 8 456*0 20 0 0 10 4*0 40 0 0 40 0 0 0 2 0 0
  //   0 2 0 0 0 8 232*0 20 0 0 10 4*0 40 0 0 40 0 0 0 2 0 0 0 8 0 0 0 8 232*0 20 0 0 10 4*0 40 0 0 40 0 0
  //   0 1 0 0 0 1 0 0 0 8 232*0 20 0 0 10 4*0 40 0 0 40 0 0 0 1 0 0 0 4 0 0 0 8 234*0 2 4*0 2 0 0 4 80 6*0
  //   2 4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
  //   CE
endmodule

module Controller_rev2 (
  input  [7:0] DATA,
  input  ENABLE,
  output [7:0] out_3
);

  wire and_1_out, and_2_out, CLOCK, CLOCK_8X, n74161_clockfix_1_q2, not_1_out, ROM_ENABLE, RUNNING;

  Clock clock_1 (.out(CLOCK_8X));
  Clock_Divider clock_divider_1 (.CLOCK(CLOCK_8X), .CLOCK_DIV8(CLOCK));  // open: CLOCK_DIV64
  not not_1 (not_1_out, RUNNING);
  and and_1 (and_1_out, not_1_out, CLOCK);
  _74161_Clockfix u_74161_clockfix_1 (
    .CLK(and_1_out), .CLR(1'b1), .LE(1'b1), .CEP(1'b1), .CET(1'b1), .D1(1'b0), .D2(1'b0), .D3(1'b0),
    .D4(1'b0), .Q2(n74161_clockfix_1_q2), .Q3(RUNNING));  // open: Q1, Q4, TC
  and and_2 (and_2_out, CLOCK_8X, ENABLE);
  // IC_74273 ic_74273_1: pin names not known; wires that end beside it: DATA[0], DATA[1], DATA[2], DATA[3], DATA[4], DATA[5], DATA[6], DATA[7], and_2_out, RUNNING, out_3[0], out_3[1], out_3[2], out_3[3], out_3[4], out_3[5], out_3[6], out_3[7]
  // DIP_7474 dip_7474_1: pin names not known; wires that end beside it: 1'b1, 1'b1, n74161_clockfix_1_q2, ROM_ENABLE

  // Notes on the sheet:
  //   Power-up delay:. Start controller after 4 clock cycles
endmodule

module Register (
  input  [7:0] DATA_BUS_IN,
  input  CLOCK,
  input  nDATA_LOAD,
  input  nDATA_OUT,
  output [7:0] CONTENTS_BUS_OUT,
  output [7:0] DATA_BUS_OUT
);

  // IC_74377 ic_74377_1: pin names not known; wires that end beside it: CLOCK, nDATA_LOAD, CONTENTS_BUS_OUT[0], CONTENTS_BUS_OUT[1], CONTENTS_BUS_OUT[2], CONTENTS_BUS_OUT[3], CONTENTS_BUS_OUT[4], CONTENTS_BUS_OUT[5], CONTENTS_BUS_OUT[6], CONTENTS_BUS_OUT[7]
  // IC_74244 ic_74244_1: pin names not known; wires that end beside it: CONTENTS_BUS_OUT[0], CONTENTS_BUS_OUT[1], CONTENTS_BUS_OUT[2], CONTENTS_BUS_OUT[3], CONTENTS_BUS_OUT[4], CONTENTS_BUS_OUT[5], CONTENTS_BUS_OUT[6], CONTENTS_BUS_OUT[7], nDATA_OUT, nDATA_OUT, DATA_BUS_OUT[0], DATA_BUS_OUT[1], DATA_BUS_OUT[2], DATA_BUS_OUT[3], DATA_BUS_OUT[4], DATA_BUS_OUT[5], DATA_BUS_OUT[6], DATA_BUS_OUT[7]
endmodule

module Flags_Register (
  input  CLOCK,
  input  Fgt_IN,
  input  Fz_IN,
  input  Fgt_LOAD,
  input  Fz_LOAD,
  input  Flt_IN,
  input  Flt_LOAD,
  input  Fc_CLEAR,
  input  Feq_IN,
  input  Feq_LOAD,
  input  Fc_LOAD,
  input  Fc_IN,
  input  Fc_SET,
  output Fcmp_OUT,
  output Fz_OUT,
  output Fc_OUT
);

  wire and_1_out, and_2_out, and_3_out, and_4_out, and_5_out, dip_7474_1_p7, not_1_out, or_1_out, or_2_out,
       or_3_out, or_4_out;

  and and_1 (and_1_out, Fgt_IN, Fgt_LOAD);
  and and_2 (and_2_out, Flt_IN, Flt_LOAD);
  and and_3 (and_3_out, Feq_IN, Feq_LOAD);
  or or_1 (or_1_out, and_1_out, and_2_out, and_3_out);
  or or_2 (or_2_out, Fgt_LOAD, Flt_LOAD, Feq_LOAD);
  and and_4 (and_4_out, or_2_out, CLOCK);
  not not_1 (not_1_out, Fc_CLEAR);
  or or_3 (or_3_out, Fc_LOAD, Fc_SET);
  and and_5 (and_5_out, or_3_out, CLOCK);
  // DIP_7474 dip_7474_1: pin names not known; wires that end beside it: 1'b1, or_1_out, and_4_out, Fcmp_OUT, 1'b1, Fz_IN, dip_7474_1_p7, Fz_OUT
  and and_6 (dip_7474_1_p7, Fz_LOAD, CLOCK);
  or or_4 (or_4_out, Fc_IN, Fc_SET);
  // DIP_7474 dip_7474_2: pin names not known; wires that end beside it: not_1_out, or_4_out, and_5_out, Fc_OUT
endmodule

module Program_Counter (
  input  PC_INC,
  input  PC_DEC,
  input  CLOCK,
  input  [7:0] PC_L_DATA_IN,
  input  nPC_L_OUT,
  input  nPC_L_LOAD,
  input  nPC_MAR_OUT,
  input  [7:0] PC_H_DATA_IN,
  input  nPC_H_OUT,
  input  nPC_H_LOAD,
  output [15:0] PC_CONTENTS,
  output [7:0] PC_L_DATA_OUT,
  output [15:0] MAR_BUS_OUT,
  output [7:0] PC_H_DATA_OUT
);

  wire DOWN_nUP, n74191_1_nrco, n74191_2_nrco, n74191_3_nrco, nCLK_EN, nor_2_out;

  nor nor_1 (DOWN_nUP, PC_INC, nor_2_out);
  nor nor_2 (nor_2_out, DOWN_nUP, PC_DEC);
  nor nor_3 (nCLK_EN, PC_INC, PC_DEC);
  _74191 u_74191_1 (
    .nU_D(DOWN_nUP), .CK(CLOCK), .nCTEN(nCLK_EN), .nPL(nPC_L_LOAD), .Q0(PC_CONTENTS[0]), .Q1(PC_CONTENTS[1]),
    .Q2(PC_CONTENTS[2]), .Q3(PC_CONTENTS[3]), .D0(PC_L_DATA_IN[0]), .D1(PC_L_DATA_IN[1]),
    .D2(PC_L_DATA_IN[2]), .D3(PC_L_DATA_IN[3]), .nRCO(n74191_1_nrco));  // open: TC
  _74191 u_74191_2 (
    .nU_D(DOWN_nUP), .CK(n74191_1_nrco), .nCTEN(nCLK_EN), .nPL(nPC_L_LOAD), .Q0(PC_CONTENTS[4]),
    .Q1(PC_CONTENTS[5]), .Q2(PC_CONTENTS[6]), .Q3(PC_CONTENTS[7]), .D0(PC_L_DATA_IN[4]),
    .D1(PC_L_DATA_IN[5]), .D2(PC_L_DATA_IN[6]), .D3(PC_L_DATA_IN[7]), .nRCO(n74191_2_nrco));  // open: TC
  _74191 u_74191_3 (
    .nU_D(DOWN_nUP), .CK(n74191_2_nrco), .nCTEN(nCLK_EN), .nPL(nPC_H_LOAD), .Q0(PC_CONTENTS[8]),
    .Q1(PC_CONTENTS[9]), .Q2(PC_CONTENTS[10]), .Q3(PC_CONTENTS[11]), .D0(PC_H_DATA_IN[0]),
    .D1(PC_H_DATA_IN[1]), .D2(PC_H_DATA_IN[2]), .D3(PC_H_DATA_IN[3]), .nRCO(n74191_3_nrco));  // open: TC
  _74191 u_74191_4 (
    .nU_D(DOWN_nUP), .CK(n74191_3_nrco), .nCTEN(nCLK_EN), .nPL(nPC_H_LOAD), .Q0(PC_CONTENTS[12]),
    .Q1(PC_CONTENTS[13]), .Q2(PC_CONTENTS[14]), .Q3(PC_CONTENTS[15]), .D0(PC_H_DATA_IN[4]),
    .D1(PC_H_DATA_IN[5]), .D2(PC_H_DATA_IN[6]), .D3(PC_H_DATA_IN[7]));  // open: TC, nRCO
  // IC_74244 ic_74244_1: pin names not known; wires that end beside it: PC_CONTENTS[0], PC_CONTENTS[1], PC_CONTENTS[2], PC_CONTENTS[3], PC_CONTENTS[4], PC_CONTENTS[5], PC_CONTENTS[6], PC_CONTENTS[7], nPC_L_OUT, nPC_L_OUT, PC_L_DATA_OUT[0], PC_L_DATA_OUT[1], PC_L_DATA_OUT[2], PC_L_DATA_OUT[3], PC_L_DATA_OUT[4], PC_L_DATA_OUT[5], PC_L_DATA_OUT[6], PC_L_DATA_OUT[7]
  // IC_74244 ic_74244_2: pin names not known; wires that end beside it: PC_CONTENTS[8], PC_CONTENTS[9], PC_CONTENTS[10], PC_CONTENTS[11], PC_CONTENTS[12], PC_CONTENTS[13], PC_CONTENTS[14], PC_CONTENTS[15], nPC_H_OUT, nPC_H_OUT, PC_H_DATA_OUT[0], PC_H_DATA_OUT[1], PC_H_DATA_OUT[2], PC_H_DATA_OUT[3], PC_H_DATA_OUT[4], PC_H_DATA_OUT[5], PC_H_DATA_OUT[6], PC_H_DATA_OUT[7]
  // IC_74244 Low_byte: pin names not known; wires that end beside it: PC_CONTENTS[0], PC_CONTENTS[1], PC_CONTENTS[2], PC_CONTENTS[3], PC_CONTENTS[4], PC_CONTENTS[5], PC_CONTENTS[6], PC_CONTENTS[7], MAR_BUS_OUT[0], MAR_BUS_OUT[1], MAR_BUS_OUT[2], MAR_BUS_OUT[3], MAR_BUS_OUT[4], MAR_BUS_OUT[5], MAR_BUS_OUT[6], MAR_BUS_OUT[7], MAR_BUS_OUT
  // IC_74244 High_byte: pin names not known; wires that end beside it: nPC_MAR_OUT, nPC_MAR_OUT, PC_CONTENTS[8], PC_CONTENTS[9], PC_CONTENTS[10], PC_CONTENTS[11], PC_CONTENTS[12], PC_CONTENTS[13], PC_CONTENTS[14], PC_CONTENTS[15], nPC_MAR_OUT, nPC_MAR_OUT, MAR_BUS_OUT[8], MAR_BUS_OUT[9], MAR_BUS_OUT[10], MAR_BUS_OUT[11], MAR_BUS_OUT[12], MAR_BUS_OUT[13], MAR_BUS_OUT[14], MAR_BUS_OUT[15]

  // Notes on the sheet:
  //   Output to address bus
endmodule

module Stack_Pointer (
  input  STK_INC,
  input  STK_DEC,
  input  CLOCK,
  input  nSTK_RESET,
  input  nSTK_OUT,
  output [15:0] STK_CONTENTS,
  output [15:0] MAR_BUS_OUT
);

  wire DOWN_nUP, n74191_1_nrco, nCLK_EN, nor_2_out;

  nor nor_1 (DOWN_nUP, STK_INC, nor_2_out);
  nor nor_2 (nor_2_out, DOWN_nUP, STK_DEC);
  nor nor_3 (nCLK_EN, STK_INC, STK_DEC);
  _74191 u_74191_1 (
    .nU_D(DOWN_nUP), .CK(CLOCK), .nCTEN(nCLK_EN), .nPL(nSTK_RESET), .Q0(STK_CONTENTS[0]),
    .Q1(STK_CONTENTS[1]), .Q2(STK_CONTENTS[2]), .Q3(STK_CONTENTS[3]), .D0(1'b0), .D1(1'b0), .D2(1'b0),
    .D3(1'b0), .nRCO(n74191_1_nrco));  // open: TC
  _74191 u_74191_2 (
    .nU_D(DOWN_nUP), .CK(n74191_1_nrco), .nCTEN(nCLK_EN), .nPL(nSTK_RESET), .Q0(STK_CONTENTS[4]),
    .Q1(STK_CONTENTS[5]), .Q2(STK_CONTENTS[6]), .Q3(STK_CONTENTS[7]), .D0(1'b0), .D1(1'b0), .D2(1'b0),
    .D3(1'b0));  // open: TC, nRCO
  // IC_74244 Low_byte: pin names not known; wires that end beside it: STK_CONTENTS[0], STK_CONTENTS[1], STK_CONTENTS[2], STK_CONTENTS[3], STK_CONTENTS[4], STK_CONTENTS[5], STK_CONTENTS[6], STK_CONTENTS[7], MAR_BUS_OUT[0], MAR_BUS_OUT[1], MAR_BUS_OUT[2], MAR_BUS_OUT[3], MAR_BUS_OUT[4], MAR_BUS_OUT[5], MAR_BUS_OUT[6], MAR_BUS_OUT[7]
  // IC_74244 High_byte: pin names not known; wires that end beside it: nSTK_OUT, nSTK_OUT, 1'b1, 1'b1, 1'b1, 1'b1, 1'b1, 1'b1, 1'b1, 1'b1, nSTK_OUT, nSTK_OUT, MAR_BUS_OUT[8], MAR_BUS_OUT[9], MAR_BUS_OUT[10], MAR_BUS_OUT[11], MAR_BUS_OUT[12], MAR_BUS_OUT[13], MAR_BUS_OUT[14], MAR_BUS_OUT[15]

  assign STK_CONTENTS[15:8] = {8{1'b1}};

  // Notes on the sheet:
  //   Output to address bus
endmodule

module ALU (
  input  SHR,
  input  [7:0] DATA_BUS_IN,
  input  CLOCK,
  input  nAX_IN,
  input  nAY_IN,
  input  S3,
  input  S2,
  input  S1,
  input  S0,
  input  M,
  input  Cn,
  input  nALU_OUT,
  output [7:0] ALU_AX_CONTENTS,
  output [7:0] ALU_AY_CONTENTS,
  output Flt,
  output Feq,
  output Fgt,
  output [7:0] DATA_BUS_OUT,
  output [7:0] CONTENTS_BUS_OUT,
  output Fz,
  output Fc
);

  wire ALU_OUT, and_1_out, and_2_out, and_4_out, and_6_out, n74181_1_p18, n74181_1_p19, n74181_2_p18,
       n74181_2_p19, nor_1_out, nor_2_out, not_1_out, not_2_out, not_3_out, not_4_out, not_5_out, SHRz;

  not not_1 (not_1_out, SHR);
  // IC_74377 AX: pin names not known; wires that end beside it: ALU_AX_CONTENTS[0], ALU_AX_CONTENTS[1], ALU_AX_CONTENTS[2], ALU_AX_CONTENTS[3], ALU_AX_CONTENTS[4], ALU_AX_CONTENTS[5], ALU_AX_CONTENTS[6], ALU_AX_CONTENTS[7]
  // IC_74377 AY: pin names not known; wires that end beside it: CLOCK, nAX_IN, CLOCK, nAY_IN, ALU_AY_CONTENTS[0], ALU_AY_CONTENTS[1], ALU_AY_CONTENTS[2], ALU_AY_CONTENTS[3], ALU_AY_CONTENTS[4], ALU_AY_CONTENTS[5], ALU_AY_CONTENTS[6], ALU_AY_CONTENTS[7]
  // _74181 74181_1: pin names not known; wires that end beside it: ALU_AY_CONTENTS[0], ALU_AX_CONTENTS[0], S3, S2, S1, S0, Cn, M, CONTENTS_BUS_OUT[0], CONTENTS_BUS_OUT[1], CONTENTS_BUS_OUT[2], ALU_AX_CONTENTS[1], ALU_AY_CONTENTS[1], ALU_AX_CONTENTS[2], ALU_AY_CONTENTS[2], ALU_AX_CONTENTS[3], ALU_AY_CONTENTS[3], n74181_1_p18, n74181_1_p19, CONTENTS_BUS_OUT[3]
  // _74181 74181_2: pin names not known; wires that end beside it: ALU_AY_CONTENTS[4], ALU_AX_CONTENTS[4], S3, S2, S1, S0, n74181_1_p18, M, CONTENTS_BUS_OUT[4], CONTENTS_BUS_OUT[5], CONTENTS_BUS_OUT[6], ALU_AX_CONTENTS[5], ALU_AY_CONTENTS[5], ALU_AX_CONTENTS[6], ALU_AY_CONTENTS[6], ALU_AX_CONTENTS[7], ALU_AY_CONTENTS[7], n74181_2_p18, n74181_2_p19, CONTENTS_BUS_OUT[7]
  // IC_74244 ic_74244_1: pin names not known; wires that end beside it: ALU_AX_CONTENTS[1], ALU_AX_CONTENTS[2], ALU_AX_CONTENTS[3], ALU_AX_CONTENTS[4], ALU_AX_CONTENTS[5], ALU_AX_CONTENTS[6], ALU_AX_CONTENTS[7], 1'b0, not_1_out, not_1_out, DATA_BUS_OUT[0], DATA_BUS_OUT[1], DATA_BUS_OUT[2], DATA_BUS_OUT[3], DATA_BUS_OUT[4], DATA_BUS_OUT[5], DATA_BUS_OUT[6], DATA_BUS_OUT[7]
  not not_2 (not_2_out, n74181_2_p18);
  and and_1 (and_1_out, SHR, ALU_AX_CONTENTS[0]);
  and and_2 (and_2_out, n74181_1_p18, n74181_2_p18);
  or or_1 (Flt, and_2_out, n74181_2_p18);
  and and_3 (Feq, n74181_1_p19, n74181_2_p19);
  not not_3 (not_3_out, n74181_1_p18);
  not not_4 (not_4_out, n74181_2_p18);
  or or_2 (Fc, not_2_out, and_1_out);
  and and_4 (and_4_out, not_3_out, not_4_out);
  or or_3 (Fgt, and_4_out, not_4_out);
  nor nor_1 (nor_1_out, CONTENTS_BUS_OUT[0], CONTENTS_BUS_OUT[1], CONTENTS_BUS_OUT[2], CONTENTS_BUS_OUT[3], CONTENTS_BUS_OUT[4], CONTENTS_BUS_OUT[5], CONTENTS_BUS_OUT[6], CONTENTS_BUS_OUT[7]);
  nor nor_2 (nor_2_out, DATA_BUS_OUT[0], DATA_BUS_OUT[1], DATA_BUS_OUT[2], DATA_BUS_OUT[3], DATA_BUS_OUT[4], DATA_BUS_OUT[5], DATA_BUS_OUT[6], DATA_BUS_OUT[7]);
  and and_5 (SHRz, nor_2_out, SHR);
  and and_6 (and_6_out, nor_1_out, not_5_out);
  not not_5 (not_5_out, SHR);
  or or_4 (Fz, and_6_out, SHRz);
  not not_6 (ALU_OUT, nALU_OUT);
  // IC_74244 ic_74244_2: pin names not known; wires that end beside it: CONTENTS_BUS_OUT[0], CONTENTS_BUS_OUT[1], CONTENTS_BUS_OUT[2], CONTENTS_BUS_OUT[3], CONTENTS_BUS_OUT[4], CONTENTS_BUS_OUT[5], CONTENTS_BUS_OUT[6], CONTENTS_BUS_OUT[7], nALU_OUT, nALU_OUT, DATA_BUS_OUT[0], DATA_BUS_OUT[1], DATA_BUS_OUT[2], DATA_BUS_OUT[3], DATA_BUS_OUT[4], DATA_BUS_OUT[5], DATA_BUS_OUT[6], DATA_BUS_OUT[7]

  // Other names for the same wires on the sheet: SHRc = ALU_AX_CONTENTS[0]

  // Notes on the sheet:
  //   M=0   Cn=0   S=0110  (A < B)
  //   M=0   Cn=1   S=0110  (A=B)
  //   M=0   Cn=1   S=0110  (A>B)
endmodule

module Memory_Access_Register (
  input  [7:0] LB_DATA_IN,
  input  CLOCK,
  input  nLB_LOAD,
  input  [7:0] HB_DATA_IN,
  input  nHB_LOAD,
  input  nZP_LOAD,
  input  nPC_MAR_OUT,
  input  nSTK_MAR_OUT,
  input  [15:0] DATA_IN,
  output [15:0] DATA_OUT
);

  wire and_2_out, nHIGH_LOAD, nLOW_LOAD, nSTK_PC_OUT;

  // IC_74244 Low_byte: pin names not known; wires that end beside it: LB_DATA_IN[0], LB_DATA_IN[1], LB_DATA_IN[2], LB_DATA_IN[3], LB_DATA_IN[4], LB_DATA_IN[5], LB_DATA_IN[6], LB_DATA_IN[7], DATA_IN[0], DATA_IN[1], DATA_IN[2], DATA_IN[3], DATA_IN[4], DATA_IN[5], DATA_IN[6], DATA_IN[7]
  // IC_74244 High_byte: pin names not known; wires that end beside it: nLB_LOAD, nLB_LOAD, HB_DATA_IN[0], HB_DATA_IN[1], HB_DATA_IN[2], HB_DATA_IN[3], HB_DATA_IN[4], HB_DATA_IN[5], HB_DATA_IN[6], HB_DATA_IN[7], nHB_LOAD, DATA_IN[8], DATA_IN[9], DATA_IN[10], DATA_IN[11], DATA_IN[12], DATA_IN[13], DATA_IN[14], DATA_IN[15]
  // IC_74244 High_byte_2: pin names not known; wires that end beside it: nHB_LOAD, 1'b0, 1'b1, 1'b1, 1'b1, 1'b1, 1'b1, 1'b1, 1'b1, nZP_LOAD, nZP_LOAD, DATA_IN[8], DATA_IN[9], DATA_IN[10], DATA_IN[11], DATA_IN[12], DATA_IN[13], DATA_IN[14], DATA_IN[15]
  // IC_74377 Low_byte_2: pin names not known; wires that end beside it: DATA_IN[0], DATA_IN[1], DATA_IN[2], DATA_IN[3], DATA_IN[4], DATA_IN[5], DATA_IN[6], DATA_IN[7], DATA_OUT[0], DATA_OUT[1], DATA_OUT[2], DATA_OUT[3], DATA_OUT[4], DATA_OUT[5], DATA_OUT[6], DATA_OUT[7]
  // IC_74377 High_byte_3: pin names not known; wires that end beside it: CLOCK, nLOW_LOAD, DATA_IN[8], DATA_IN[9], DATA_IN[10], DATA_IN[11], DATA_IN[12], DATA_IN[13], DATA_IN[14], DATA_IN[15], CLOCK, nHIGH_LOAD, DATA_OUT[8], DATA_OUT[9], DATA_OUT[10], DATA_OUT[11], DATA_OUT[12], DATA_OUT[13], DATA_OUT[14], DATA_OUT[15]
  and and_1 (nLOW_LOAD, nLB_LOAD, nSTK_PC_OUT);
  and and_2 (and_2_out, nHB_LOAD, nZP_LOAD);
  and and_3 (nHIGH_LOAD, and_2_out, nSTK_PC_OUT);
  and and_4 (nSTK_PC_OUT, nPC_MAR_OUT, nSTK_MAR_OUT);

  // Notes on the sheet:
  //   Input from data bus
  //   Zero page offset
endmodule

module Memory (
  input  BOOT_ROM,
  input  PROGRAM_RAM,
  input  nRAM_LOAD,
  input  nMEM_OUT,
  input  CLOCK,
  input  [15:0] ADDRESS_IN,
  input  [7:0] DATA_IN,
  input  [7:0] MANUAL_DATA_IN,
  output [7:0] CONTENTS_OUT,
  output [7:0] DATA_OUT
);

  wire nMEM_OUT_t, nor_1_out, nor_3_out, not_2_out, not_3_out, not_4_out, not_5_out, nRAM_CE, nRAM_WE,
       nROM_CE;

  not not_1 (nRAM_CE, nROM_CE);
  nor nor_1 (nor_1_out, ADDRESS_IN[14], ADDRESS_IN[15]);
  nand nand_1 (nROM_CE, nor_1_out, BOOT_ROM);
  not not_2 (not_2_out, nRAM_CE);
  not not_3 (not_3_out, nROM_CE);
  RAM #(.addrWidth(16)) ram_1 (
    .addr(ADDRESS_IN), .data(CONTENTS_OUT), .sel(not_2_out), .clk(CLOCK), .ld(nRAM_WE), .clr(1'b0));
  ROM #(.addrWidth(16)) rom_1 (.addr(ADDRESS_IN), .data(CONTENTS_OUT), .sel(not_3_out));
  nor nor_2 (nMEM_OUT_t, nor_3_out, nor_3_out);
  nor nor_3 (nor_3_out, PROGRAM_RAM, nMEM_OUT);
  not not_4 (not_4_out, PROGRAM_RAM);
  // IC_74244 ic_74244_1: pin names not known; wires that end beside it: CONTENTS_OUT[0], CONTENTS_OUT[1], CONTENTS_OUT[2], CONTENTS_OUT[3], CONTENTS_OUT[4], CONTENTS_OUT[5], CONTENTS_OUT[6], CONTENTS_OUT[7], DATA_OUT[0], DATA_OUT[1], DATA_OUT[2], DATA_OUT[3], DATA_OUT[4], DATA_OUT[5], DATA_OUT[6], DATA_OUT[7]
  // IC_74244 ic_74244_2: pin names not known; wires that end beside it: nMEM_OUT_t, nMEM_OUT_t, DATA_IN[0], DATA_IN[1], DATA_IN[2], DATA_IN[3], DATA_IN[4], DATA_IN[5], DATA_IN[6], CONTENTS_OUT[0], CONTENTS_OUT[1], CONTENTS_OUT[2], CONTENTS_OUT[3], CONTENTS_OUT[4], CONTENTS_OUT[5], CONTENTS_OUT[6]
  // IC_74244 ic_74244_3: pin names not known; wires that end beside it: DATA_IN[7], nRAM_LOAD, nRAM_LOAD, MANUAL_DATA_IN[0], MANUAL_DATA_IN[1], MANUAL_DATA_IN[2], MANUAL_DATA_IN[3], MANUAL_DATA_IN[4], MANUAL_DATA_IN[5], MANUAL_DATA_IN[6], MANUAL_DATA_IN[7], not_4_out, not_4_out, CONTENTS_OUT[7], CONTENTS_OUT[0], CONTENTS_OUT[1], CONTENTS_OUT[2], CONTENTS_OUT[3], CONTENTS_OUT[4], CONTENTS_OUT[5], CONTENTS_OUT[6], CONTENTS_OUT[7]
  not not_5 (not_5_out, nRAM_LOAD);
  nor nor_4 (nRAM_WE, PROGRAM_RAM, not_5_out);

  // Notes on the sheet:
  //   Toggle output/input from/to memory chips
  //   RAM
  //   ROM
  //   contents of rom_1 (hex, n*v repeats v):
  //   e aa 2 3 4 55 59 f bb 5 6 7 56 5a 10 cc 8 9 a 57 5b 11 dd b c d 58 5c 3d a0 3e a1 12 30 0 13 30 1 71
  //   30 2 72 30 3 6a 30 4 6b 30 5 e aa 16 40 0 f bb 17 40 1 12 40 1 13 40 0 e 3 60 0 f 4 79 1 77 1 78 0
  //   74 1 73 0 11 30 10 10 6d 6e 82 83 75 11 30 10 10 76 11 40 10 0 e aa 6f 11 40 10 1 f bb 70 12 40 1 13
  //   40 0 10 10 e aa 7e 7b 10 11 f bb 7f 7a 7b 7d 7c 85 84 e 30 16 40 0 e 10 16 40 1 6a 40 0 3e 0 71 40 1
  //   1c 6d 6a 40 0 3e 0 71 40 1 1c 6e 6a 40 0 3e 0 71 40 1 1c 75 6a 40 0 3e 0 71 40 1 1c 76 e 40 16 40 0
  //   e 10 16 40 1 e aa 6a 40 0 3e 0 71 40 1 1c 6f 13 40 10 e bb 6a 40 0 3e 0 71 40 1 1c 6f e 0 12 40 10 e
  //   1 94 e 2 94 e 3 94 99 99 99 f 1 95 f 2 95 f 3 95 98 98 98 10 1 96 10 2 96 10 3 96 9b 9b 9b 11 1 97
  //   11 2 97 11 3 97 9a 9a 9a e 1 94 e 2 94 e 3 94 9c 9c 9c e 1 94 e 2 94 e 3 94 9d 9d 9d 69 68 69 68 69
  //   68 3d 1 3e 2 1a 3d fa 3e fa 61 3d 1 3e 1 1e 3d 0 3e 0 1c 3d 2 3e 1 20 3e 3 63 3d 2 3e 1 24 3d 0 34
  //   55 34 55 34 3d 0 35 56 35 56 35 3d 0 36 57 36 57 36 3d 0 37 58 37 58 37 3d 3 38 55 38 55 38 3d 3 39
  //   56 39 56 39 3d 3 3a 57 3a 57 3a 3d 3 3b 58 3b 58 3b 3d ff 34 3d aa 3e 55 26 66 3d aa 3e aa 27 2b 3d
  //   aa 30 3d ff 3e 55 2d 3d 5c 14 3d bb 5e 3d bb 18 3d 1 3e 2 3c 3d 3 3e 3 3c 3d 4 3e 5 93 3d 6 93 3d 7
  //   3e 6 92 3d 6 3e 7 92 e 99 3f 1 ca 1 3d 0 3e 0 1a 40 1 d3 1 3d 1 3e 0 1a 41 1 e2 3f 1 df 1 e f1 1 3d
  //   ff 3e 3 1a 42 1 eb 1 3d 0 3e 3 1a 43 1 fa 42 1 f7 1 e f2 1 e 4 92 44 2 1 1 e 5 3c 45 2 e 44 2 b 1 e
  //   f3 1 e 6 0 0 0 e 99 e 0 e 99 e 0 e 99 e 0 3d 0 47 2 2c 3d 5 47 2 2c 3f 2 30 34 55 14 48 e 3 47 2 38
  //   3f 2 3e 55 38 8c 3f 2 38 e 99 55 3e 88 93 8a 2 4c f 55 3f 2 4f e 55 48 e 0 3e ff 31 55 3c 44 2 5d 34
  //   3f 2 53 31 55 40 2 4f 38 3f 2 5d 11674*0 aa bb cc dd a0 a1 10*0 1 2 3 4 20461*0 bb
  //   RAM write switch
endmodule

module Output_Control (
  input  nOUT2_LOAD,
  input  [7:0] DATA_BUS_IN,
  input  CLOCK,
  input  nOUT1_LOAD,
  input  CLOCK_8X,
  output [7:0] CONTENTS_BUS_OUT,
  output [6:0] TTY_DATA,
  output TTY_CLOCK,
  output TTY_WRITE
);

  wire dip_7474_1_p4, not_1_out, not_2_out;

  and and_1 (TTY_CLOCK, CLOCK_8X, dip_7474_1_p4);
  not not_1 (not_1_out, TTY_CLOCK);
  // IC_74377 ic_74377_1: pin names not known; wires that end beside it: nOUT2_LOAD, CLOCK, nOUT1_LOAD, CONTENTS_BUS_OUT[0], CONTENTS_BUS_OUT[1], CONTENTS_BUS_OUT[2], CONTENTS_BUS_OUT[3], CONTENTS_BUS_OUT[4], CONTENTS_BUS_OUT[5], CONTENTS_BUS_OUT[6], CONTENTS_BUS_OUT[7]
  not not_2 (not_2_out, nOUT1_LOAD);
  // DIP_7474 dip_7474_1: pin names not known; wires that end beside it: not_1_out, not_2_out, CLOCK, dip_7474_1_p4

  assign TTY_DATA = CONTENTS_BUS_OUT[6:0];
  assign TTY_WRITE = 1'b1;
endmodule

module Clock_Divider (
  input  CLOCK,
  output CLOCK_DIV8,
  output CLOCK_DIV64
);

  wire d_ff_1_q, d_ff_1_qn, d_ff_2_q, d_ff_2_qn, d_ff_3_q, d_ff_3_qn, d_ff_4_q, d_ff_4_qn, d_ff_5_q,
       d_ff_5_qn, d_ff_6_q, d_ff_6_qn, d_ff_7_q, d_ff_7_qn;

  D_Flip_Flop d_ff_1 (.clk(CLOCK), .D(d_ff_1_qn), .Q(d_ff_1_q), .Qn(d_ff_1_qn), .en(1'b1));  // open: preset, reset
  D_Flip_Flop d_ff_2 (.clk(d_ff_1_q), .D(d_ff_2_qn), .Q(d_ff_2_q), .Qn(d_ff_2_qn), .en(1'b1));  // open: preset, reset
  D_Flip_Flop d_ff_3 (.clk(d_ff_2_q), .D(d_ff_3_qn), .Q(d_ff_3_q), .Qn(d_ff_3_qn), .en(1'b1));  // open: preset, reset
  D_Flip_Flop d_ff_4 (.clk(d_ff_3_q), .D(d_ff_4_qn), .Q(d_ff_4_q), .Qn(d_ff_4_qn), .en(1'b1));  // open: preset, reset
  not not_1 (CLOCK_DIV8, d_ff_4_q);
  D_Flip_Flop d_ff_5 (.clk(d_ff_4_q), .D(d_ff_5_qn), .Q(d_ff_5_q), .Qn(d_ff_5_qn), .en(1'b1));  // open: preset, reset
  D_Flip_Flop d_ff_6 (.clk(d_ff_7_q), .D(d_ff_6_qn), .Q(d_ff_6_q), .Qn(d_ff_6_qn), .en(1'b1));  // open: preset, reset
  D_Flip_Flop d_ff_7 (.clk(d_ff_5_q), .D(d_ff_7_qn), .Q(d_ff_7_q), .Qn(d_ff_7_qn), .en(1'b1));  // open: preset, reset
  not not_2 (CLOCK_DIV64, d_ff_6_q);
endmodule

// 74161
module _74161_Clockfix (
  input  CLK,
  input  CLR,
  input  LE,
  input  CEP,
  input  CET,
  input  D1,
  input  D2,
  input  D3,
  input  D4,
  output Q1,
  output Q2,
  output Q3,
  output Q4,
  output TC
);

  wire and_1_out, and_2_out, and_3_out, and_4_out, and_5_out, and_6_out, and_7_out, and_8_out, and_9_out,
       and_10_out, and_11_out, and_12_out, not_1_out, not_2_out, or_1_out, or_2_out, or_3_out, or_4_out,
       xor_1_out, xor_2_out, xor_3_out, xor_4_out;

  not not_1 (not_1_out, CLR);
  and and_1 (and_1_out, LE, CEP, CET);
  not not_2 (not_2_out, LE);
  and and_2 (and_2_out, D1, not_2_out);
  and and_3 (and_3_out, Q1, LE);
  and and_4 (and_4_out, D2, not_2_out);
  and and_5 (and_5_out, Q2, LE);
  and and_6 (and_6_out, Q1, and_1_out);
  and and_7 (and_7_out, D3, not_2_out);
  and and_8 (and_8_out, Q3, LE);
  and and_9 (and_9_out, Q2, Q1, and_1_out);
  and and_10 (and_10_out, D4, not_2_out);
  and and_11 (and_11_out, Q4, LE);
  and and_12 (and_12_out, Q3, Q2, Q1, and_1_out);
  xor xor_1 (xor_1_out, and_3_out, and_1_out);
  xor xor_2 (xor_2_out, and_5_out, and_6_out);
  xor xor_3 (xor_3_out, and_8_out, and_9_out);
  xor xor_4 (xor_4_out, and_11_out, and_12_out);
  or or_1 (or_1_out, and_2_out, xor_1_out);
  or or_2 (or_2_out, and_4_out, xor_2_out);
  or or_3 (or_3_out, and_7_out, xor_3_out);
  or or_4 (or_4_out, and_10_out, xor_4_out);
  // D_Flip_Flop d_flip_flop_1: pin names not known; wires that end beside it: or_1_out, CLK, not_1_out, Q1
  // D_Flip_Flop d_flip_flop_2: pin names not known; wires that end beside it: or_2_out, CLK, not_1_out, Q2
  // D_Flip_Flop d_flip_flop_3: pin names not known; wires that end beside it: or_3_out, CLK, not_1_out, Q3
  // D_Flip_Flop d_flip_flop_4: pin names not known; wires that end beside it: or_4_out, CLK, not_1_out, Q4
  and and_13 (TC, Q4, Q3, Q2, Q1, CET);
endmodule

module LCD_Decoder (
  input  [7:0] DATA,
  input  CLOCK,
  input  nLOAD,
  output RESET,
  output [15:0] COLOR,
  output LCD_CLOCK,
  output [6:0] X_COORD,
  output [6:0] Y_COORD
);

  wire and_1_out, and_3_out, dip_7474_1_p4, dip_7474_1_p5, n74191_1_nrco, n74191_2_nrco, n74191_3_nrco,
       n74191_3_q3, n74191_4_q0, n74191_4_q1, nand_1_out, not_1_out, not_3_out, not_4_out, RESET_t;
  wire [7:5] ic_74377_1_p16;

  Pull_Resistor pull_resistor_1 (.node(DATA[0]));
  not not_1 (not_1_out, CLOCK);
  // IC_74377 ic_74377_1: pin names not known; wires that end beside it: DATA[0], DATA[1], DATA[2], DATA[3], DATA[4], DATA[5], DATA[6], DATA[7], not_1_out, nLOAD, COLOR[5], COLOR[6], COLOR[7], COLOR[8], COLOR[9], ic_74377_1_p16[5], ic_74377_1_p16[6], ic_74377_1_p16[7]
  and and_1 (and_1_out, ic_74377_1_p16[7], ic_74377_1_p16[6], ic_74377_1_p16[5], COLOR[9], COLOR[8], COLOR[7], COLOR[6], COLOR[5]);
  not not_2 (RESET_t, RESET);
  and and_2 (RESET, and_1_out, not_3_out);
  not not_3 (not_3_out, nLOAD);
  nand nand_1 (nand_1_out, CLOCK, nLOAD);
  and and_3 (and_3_out, CLOCK, not_3_out);
  and and_4 (LCD_CLOCK, RESET_t, dip_7474_1_p4);
  not not_4 (not_4_out, dip_7474_1_p4);
  // DIP_7474 dip_7474_1: pin names not known; wires that end beside it: nand_1_out, and_3_out, and_3_out, dip_7474_1_p4, dip_7474_1_p5
  _74191 u_74191_1 (
    .nU_D(1'b0), .CK(not_4_out), .nCTEN(1'b0), .nPL(RESET_t), .Q0(X_COORD[0]), .Q1(X_COORD[1]),
    .Q2(X_COORD[2]), .Q3(X_COORD[3]), .D0(1'b0), .D1(1'b0), .D2(1'b0), .D3(1'b0), .nRCO(n74191_1_nrco));  // open: TC
  _74191 u_74191_2 (
    .nU_D(1'b0), .CK(n74191_1_nrco), .nCTEN(1'b0), .nPL(RESET_t), .Q0(X_COORD[4]), .Q1(Y_COORD[0]),
    .Q2(Y_COORD[1]), .Q3(Y_COORD[2]), .D0(1'b0), .D1(1'b0), .D2(1'b0), .D3(1'b0), .nRCO(n74191_2_nrco));  // open: TC
  _74191 u_74191_3 (
    .nU_D(1'b0), .CK(n74191_2_nrco), .nCTEN(1'b0), .nPL(RESET_t), .Q0(Y_COORD[3]), .Q1(Y_COORD[4]),
    .Q2(dip_7474_1_p5), .Q3(n74191_3_q3), .D0(1'b0), .D1(1'b0), .D2(1'b0), .D3(1'b0), .nRCO(n74191_3_nrco));  // open: TC
  _74191 u_74191_4 (
    .nU_D(1'b0), .CK(n74191_3_nrco), .nCTEN(1'b0), .nPL(RESET_t), .Q0(n74191_4_q0), .Q1(n74191_4_q1),
    .D0(1'b0), .D1(1'b0), .D2(1'b0), .D3(1'b0));  // open: Q2, Q3, TC, nRCO

  assign {COLOR[15:10], COLOR[4:0]} = {11{1'b0}};
  assign X_COORD[6:5] = 2'b00;
  assign Y_COORD[6:5] = 2'b00;
endmodule

module Test (
  input  PROGRAM_RAM,
  input  nRAM_LOAD,
  input  CLOCK
);

  wire nor_1_out, not_1_out, nRAM_WE;

  not not_1 (not_1_out, nRAM_LOAD);
  nor nor_1 (nor_1_out, PROGRAM_RAM, not_1_out);
  or or_1 (nRAM_WE, nor_1_out, CLOCK);

  // Notes on the sheet:
  //   RAM write switch
endmodule
